// Logisim project block_diagram.circ as structural Verilog: 2 circuits, main circuit main
module main (
  input  [2:0] S2_S1_S0,
  input  [3:0] B3_B2_B1_B0,
  input  [3:0] A3_A2_A1_A0,
  output [3:0] O3_O2_O1_O0,
  output [3:0] V_Z_S_C
);

  ALU alu_1 (
    .B3(B3_B2_B1_B0[3]), .B2(B3_B2_B1_B0[2]), .B1(B3_B2_B1_B0[1]), .B0(B3_B2_B1_B0[0]), .A3(A3_A2_A1_A0[3]),
    .A2(A3_A2_A1_A0[2]), .A1(A3_A2_A1_A0[1]), .A0(A3_A2_A1_A0[0]), .S2(S2_S1_S0[2]), .S1(S2_S1_S0[1]),
    .S0(S2_S1_S0[0]), .O3(O3_O2_O1_O0[3]), .O2(O3_O2_O1_O0[2]), .O1(O3_O2_O1_O0[1]), .O0(O3_O2_O1_O0[0]),
    .V(V_Z_S_C[3]), .Z(V_Z_S_C[2]), .S(V_Z_S_C[1]), .C(V_Z_S_C[0]));

  // Notes on the sheet:
  //   4-bit input B
  //   4-bit input A
  //   control/selection
  //   bits
  //   4-BIT ALU
  //   4-bit output O
  //   Status Flags
endmodule

module ALU (
  input  S2,
  input  S1,
  input  S0,
  input  B3,
  input  B2,
  input  B1,
  input  B0,
  input  A3,
  input  A2,
  input  A1,
  input  A0,
  output O3,
  output O2,
  output O1,
  output O0,
  output V,
  output Z,
  output S,
  output C
);

  wire adder_1_cout, adder_2_cout, adder_3_cout, adder_4_cout, and_1_out, and_2_out, and_3_out, and_4_out,
       and_5_out, and_6_out, and_7_out, and_8_out, and_9_out, and_10_out, and_11_out, and_12_out, and_13_out,
       and_14_out, and_15_out, and_16_out, and_17_out, and_18_out, not_1_out, not_2_out, not_3_out,
       not_4_out, not_5_out, not_6_out, or_1_out, or_2_out, or_3_out, or_4_out, or_5_out, or_6_out, or_7_out,
       or_8_out, or_9_out, or_10_out, or_11_out, or_12_out;

  not not_1 (not_1_out, S2);
  not not_2 (not_2_out, S1);
  and and_1 (and_1_out, not_2_out, S2);
  or or_1 (or_1_out, not_2_out, not_1_out);
  and and_2 (and_2_out, not_2_out, not_1_out);
  and and_3 (and_3_out, S0, not_1_out);
  or or_2 (or_2_out, B0, or_1_out);
  or or_3 (or_3_out, B1, or_1_out);
  or or_4 (or_4_out, B2, or_1_out);
  or or_5 (or_5_out, B3, or_1_out);
  not not_3 (not_3_out, B0);
  and and_4 (and_4_out, or_2_out, A0);
  not not_4 (not_4_out, B1);
  and and_5 (and_5_out, or_3_out, A1);
  not not_5 (not_5_out, B2);
  and and_6 (and_6_out, or_4_out, A2);
  not not_6 (not_6_out, B3);
  and and_7 (and_7_out, or_5_out, A3);
  and and_8 (and_8_out, and_2_out, not_3_out);
  and and_9 (and_9_out, B0, and_1_out);
  and and_10 (and_10_out, and_2_out, not_4_out);
  and and_11 (and_11_out, B1, and_1_out);
  and and_12 (and_12_out, and_2_out, not_5_out);
  and and_13 (and_13_out, B2, and_1_out);
  and and_14 (and_14_out, and_2_out, not_6_out);
  and and_15 (and_15_out, B3, and_1_out);
  or or_6 (or_6_out, and_9_out, and_4_out);
  or or_7 (or_7_out, and_11_out, and_5_out);
  or or_8 (or_8_out, and_13_out, and_6_out);
  or or_9 (or_9_out, and_15_out, and_7_out);
  Adder #(.width(1)) adder_1 (.a(or_6_out), .b(and_8_out), .out(O0), .cin(and_3_out), .cout(adder_1_cout));
  and and_16 (and_16_out, adder_1_cout, not_1_out);
  Adder #(.width(1)) adder_2 (.a(or_7_out), .b(and_10_out), .out(O1), .cin(and_16_out), .cout(adder_2_cout));
  and and_17 (and_17_out, adder_2_cout, not_1_out);
  Adder #(.width(1)) adder_3 (.a(or_8_out), .b(and_12_out), .out(O2), .cin(and_17_out), .cout(adder_3_cout));
  and and_18 (and_18_out, adder_3_cout, not_1_out);
  Adder #(.width(1)) adder_4 (.a(or_9_out), .b(and_14_out), .out(O3), .cin(and_18_out), .cout(adder_4_cout));
  and and_19 (C, adder_4_cout, not_1_out);
  or or_10 (or_10_out, O0, O1);
  or or_11 (or_11_out, O2, O3);
  xor xor_1 (V, and_18_out, C);
  or or_12 (or_12_out, or_10_out, or_11_out);
  not not_7 (Z, or_12_out);

  assign S = O3;
endmodule
