// Logisim project B2_Group3.circ as structural Verilog
module main (
  input  Reset,
  output [7:0] t0,
  output [7:0] t1,
  output [7:0] t2,
  output [7:0] t3,
  output [7:0] t4,
  output [7:0] t5,
  output [7:0] sp
);

  wire Clock_out, control_unit_1_alusrc, control_unit_1_brancheq, control_unit_1_branchneq,
       control_unit_1_jump, control_unit_1_memread, control_unit_1_memtoreg, control_unit_1_memwrite,
       control_unit_1_regdst, control_unit_1_regwrite, control_unit_1_shift, mips_alu_8_bit_by_tushar_1_p4,
       multiplexer_6_out;
  wire [2:0] control_unit_1_aluop;
  wire [3:0] multiplexer_2_out;
  wire [7:0] adder_1_out, adder_2_out, mips_alu_8_bit_by_tushar_1_p5, multiplexer_1_out, multiplexer_3_out,
       multiplexer_4_out, multiplexer_5_out, multiplexer_7_out, PC_q, ram_1_data,
       register_file_1_read_data_1, register_file_1_read_data_2, rom_1_data_2;
  wire [19:0] rom_1_data;

  Register PC (.D(multiplexer_1_out), .Q(PC_q), .clk(Clock_out), .clr(Reset));  // open: en
  Clock Clock (.out(Clock_out));
  Multiplexer #(.width(8), .enable("false")) multiplexer_1 (
    .in0(multiplexer_5_out), .in1(rom_1_data_2), .out(multiplexer_1_out), .sel(control_unit_1_jump));
  Adder adder_1 (.a(PC_q), .b(8'h1), .out(adder_1_out));  // open: cin, cout
  ROM #(.dataWidth(20)) rom_1 (.addr(PC_q), .data({rom_1_data[19:16], rom_1_data_2, rom_1_data[7:0]}));  // open: sel
  Adder adder_2 (.a(adder_1_out), .b(rom_1_data[7:0]), .out(adder_2_out));  // open: cin, cout
  Multiplexer #(.width(4), .disabled(0), .enable("false")) multiplexer_2 (
    .in0(rom_1_data_2[3:0]), .in1(rom_1_data[7:4]), .out(multiplexer_2_out), .sel(control_unit_1_regdst));
  Control_Unit control_unit_1 (
    .OpCode(rom_1_data[19:16]), .RegDst(control_unit_1_regdst), .ALUSrc(control_unit_1_alusrc),
    .MemtoReg(control_unit_1_memtoreg), .MemRead(control_unit_1_memread), .MemWrite(control_unit_1_memwrite),
    .BranchEq(control_unit_1_brancheq), .BranchNeq(control_unit_1_branchneq), .Jump(control_unit_1_jump),
    .ALUOp(control_unit_1_aluop), .RegWrite(control_unit_1_regwrite), .Shift(control_unit_1_shift));
  Register_File register_file_1 (
    .Write_Data(multiplexer_7_out), .RegWrite(control_unit_1_regwrite), .Read_Register_1(rom_1_data_2[7:4]),
    .Read_Register_2(rom_1_data_2[3:0]), .Read_Data_1(register_file_1_read_data_1),
    .Read_Data_2(register_file_1_read_data_2), .Write_Register(multiplexer_2_out), .R1({t3, t2, t1, t0}),
    .R2({sp, t5, t4}), .Clock(Clock_out), .Reset(Reset));
  Multiplexer #(.width(8), .disabled(0), .enable("false")) multiplexer_3 (
    .in0(register_file_1_read_data_2), .in1(rom_1_data[7:0]), .out(multiplexer_3_out),
    .sel(control_unit_1_alusrc));
  Multiplexer #(.width(8), .disabled(0), .enable("false")) multiplexer_4 (
    .in0(register_file_1_read_data_1), .in1({4'b0000, rom_1_data[3:0]}), .out(multiplexer_4_out),
    .sel(control_unit_1_shift));
  // MIPS_ALU_8_bit_by_Tushar mips_alu_8_bit_by_tushar_1: pin names not known; wires that end beside it: multiplexer_4_out, multiplexer_3_out, control_unit_1_aluop, mips_alu_8_bit_by_tushar_1_p4, mips_alu_8_bit_by_tushar_1_p5
  Multiplexer #(.width(8), .disabled(0), .enable("false")) multiplexer_5 (
    .in0(adder_1_out), .in1(adder_2_out), .out(multiplexer_5_out), .sel(multiplexer_6_out));
  Multiplexer #(.disabled(0), .enable("false")) multiplexer_6 (
    .in0(control_unit_1_branchneq), .in1(control_unit_1_brancheq), .out(multiplexer_6_out),
    .sel(mips_alu_8_bit_by_tushar_1_p4));
  Multiplexer #(.width(8), .disabled(0), .enable("false")) multiplexer_7 (
    .in0(mips_alu_8_bit_by_tushar_1_p5), .in1(ram_1_data), .out(multiplexer_7_out),
    .sel(control_unit_1_memtoreg));
  RAM #(.bus("separate")) ram_1 (
    .addr(mips_alu_8_bit_by_tushar_1_p5), .din(register_file_1_read_data_2), .data(ram_1_data),
    .str(control_unit_1_memwrite), .clk(Clock_out), .ld(control_unit_1_memread), .clr(Reset));  // open: sel

  // Notes on the sheet:
  //   contents of rom_1 (hex, n*v repeats v):
  //   167ff 16005 90105 60130 53001 f1a00 70042 e4310 1040 c4310 21100 d1014 41003 b1103 a1111 f1900 47100
  //   97701 47000 97701 17701 b7100 17701 b7000 f1a00 301f6
  //   Register Values
endmodule

module Control_Unit (
  input  [3:0] OpCode,
  output RegDst,
  output ALUSrc,
  output MemtoReg,
  output RegWrite,
  output MemRead,
  output MemWrite,
  output BranchEq,
  output BranchNeq,
  output Shift,
  output Jump,
  output [2:0] ALUOp
);

  ROM #(.addrWidth(4), .dataWidth(13)) rom_1 (
    .addr(OpCode),
    .data({RegDst, ALUSrc, MemtoReg, RegWrite, MemRead, MemWrite, BranchEq, BranchNeq, Shift, Jump, ALUOp}));  // open: sel

  // Notes on the sheet:
  //   contents of rom_1 (hex, n*v repeats v):
  //   1202 a00 a03 21 880 41 1200 1215 1203 a01 1216 f00 1204 a02 1201 8
endmodule

// Register\nFile
module Register_File (
  input  Clock,
  input  [7:0] Write_Data,
  input  RegWrite,
  input  [3:0] Write_Register,
  input  Reset,
  input  [3:0] Read_Register_1,
  input  [3:0] Read_Register_2,
  output [23:0] R2,
  output [31:0] R1,
  output [7:0] Read_Data_1,
  output [7:0] Read_Data_2
);

  wire decoder_1_out0, decoder_1_out1, decoder_1_out2, decoder_1_out3, decoder_1_out4, decoder_1_out5,
       decoder_1_out6, decoder_1_out7;
  wire [7:0] Zero_q;

  Decoder #(.select(3), .disabled(0)) decoder_1 (
    .out0(decoder_1_out0), .out1(decoder_1_out1), .out2(decoder_1_out2), .out3(decoder_1_out3),
    .out4(decoder_1_out4), .out5(decoder_1_out5), .out6(decoder_1_out6), .out7(decoder_1_out7),
    .sel(Write_Register[2:0]), .en(RegWrite));
  Register Zero (.D({8{1'b0}}), .en(decoder_1_out6), .Q(Zero_q), .clk(Clock), .clr(Reset));
  Register t0 (.D(Write_Data), .en(decoder_1_out0), .Q(R1[7:0]), .clk(Clock), .clr(Reset));
  Multiplexer #(.select(3), .width(8), .enable("false")) multiplexer_1 (
    .in0(R1[7:0]), .in1(R1[15:8]), .in2(R1[23:16]), .in3(R1[31:24]), .in4(R2[7:0]), .in5(R2[15:8]),
    .in6(Zero_q), .in7(R2[23:16]), .out(Read_Data_1), .sel(Read_Register_1[2:0]));
  Register t1 (.D(Write_Data), .en(decoder_1_out1), .Q(R1[15:8]), .clk(Clock), .clr(Reset));
  Register t2 (.D(Write_Data), .en(decoder_1_out2), .Q(R1[23:16]), .clk(Clock), .clr(Reset));
  Register t3 (.D(Write_Data), .en(decoder_1_out3), .Q(R1[31:24]), .clk(Clock), .clr(Reset));
  Register t4 (.D(Write_Data), .en(decoder_1_out4), .Q(R2[7:0]), .clk(Clock), .clr(Reset));
  Multiplexer #(.select(3), .width(8), .disabled(0), .enable("false")) multiplexer_2 (
    .in0(R1[7:0]), .in1(R1[15:8]), .in2(R1[23:16]), .in3(R1[31:24]), .in4(R2[7:0]), .in5(R2[15:8]),
    .in6(Zero_q), .in7(R2[23:16]), .out(Read_Data_2), .sel(Read_Register_2[2:0]));
  Register t5 (.D(Write_Data), .en(decoder_1_out5), .Q(R2[15:8]), .clk(Clock), .clr(Reset));
  Register sp (.D(Write_Data), .en(decoder_1_out7), .Q(R2[23:16]), .clk(Clock), .clr(Reset));
endmodule
