// Logisim project B2_Group3.circ as structural Verilog
module Control_Unit (
  input  [3:0] OpCode,
  output RegDst,
  output ALUSrc,
  output MemtoReg,
  output RegWrite,
  output MemRead,
  output MemWrite,
  output BranchEq,
  output BranchNeq,
  output Shift,
  output Jump,
  output [2:0] ALUOp
);

  ROM #(.addrWidth(4), .dataWidth(13)) rom_1 (
    .addr(OpCode),
    .data({RegDst, ALUSrc, MemtoReg, RegWrite, MemRead, MemWrite, BranchEq, BranchNeq, Shift, Jump, ALUOp}));  // open: sel

  // Notes on the sheet:
  //   contents of rom_1 (hex, n*v repeats v):
  //   1202 a00 a03 21 880 41 1200 1215 1203 a01 1216 f00 1204 a02 1201 8
endmodule

// Register\nFile
module Register_File (
  input  Clock,
  input  [7:0] Write_Data,
  input  RegWrite,
  input  [3:0] Write_Register,
  input  Reset,
  input  [3:0] Read_Register_1,
  input  [3:0] Read_Register_2,
  output [23:0] R2,
  output [31:0] R1,
  output [7:0] Read_Data_1,
  output [7:0] Read_Data_2
);

  wire decoder_1_out0, decoder_1_out1, decoder_1_out2, decoder_1_out3, decoder_1_out4, decoder_1_out5,
       decoder_1_out6, decoder_1_out7;
  wire [7:0] Zero_q;

  Decoder #(.select(3), .disabled(0)) decoder_1 (
    .out0(decoder_1_out0), .out1(decoder_1_out1), .out2(decoder_1_out2), .out3(decoder_1_out3),
    .out4(decoder_1_out4), .out5(decoder_1_out5), .out6(decoder_1_out6), .out7(decoder_1_out7),
    .sel(Write_Register[2:0]), .en(RegWrite));
  Register Zero (.D({8{1'b0}}), .en(decoder_1_out6), .Q(Zero_q), .clk(Clock), .clr(Reset));
  Register t0 (.D(Write_Data), .en(decoder_1_out0), .Q(R1[7:0]), .clk(Clock), .clr(Reset));
  Multiplexer #(.select(3), .width(8), .enable("false")) multiplexer_1 (
    .in0(R1[7:0]), .in1(R1[15:8]), .in2(R1[23:16]), .in3(R1[31:24]), .in4(R2[7:0]), .in5(R2[15:8]),
    .in6(Zero_q), .in7(R2[23:16]), .out(Read_Data_1), .sel(Read_Register_1[2:0]));
  Register t1 (.D(Write_Data), .en(decoder_1_out1), .Q(R1[15:8]), .clk(Clock), .clr(Reset));
  Register t2 (.D(Write_Data), .en(decoder_1_out2), .Q(R1[23:16]), .clk(Clock), .clr(Reset));
  Register t3 (.D(Write_Data), .en(decoder_1_out3), .Q(R1[31:24]), .clk(Clock), .clr(Reset));
  Register t4 (.D(Write_Data), .en(decoder_1_out4), .Q(R2[7:0]), .clk(Clock), .clr(Reset));
  Multiplexer #(.select(3), .width(8), .disabled(0), .enable("false")) multiplexer_2 (
    .in0(R1[7:0]), .in1(R1[15:8]), .in2(R1[23:16]), .in3(R1[31:24]), .in4(R2[7:0]), .in5(R2[15:8]),
    .in6(Zero_q), .in7(R2[23:16]), .out(Read_Data_2), .sel(Read_Register_2[2:0]));
  Register t5 (.D(Write_Data), .en(decoder_1_out5), .Q(R2[15:8]), .clk(Clock), .clr(Reset));
  Register sp (.D(Write_Data), .en(decoder_1_out7), .Q(R2[23:16]), .clk(Clock), .clr(Reset));
endmodule

module IF_ID (
  input  [7:0] next_instruction,
  input  Clock,
  input  [19:0] Instruction,
  input  Reset,
  output [7:0] next_instruction_2,
  output [19:0] Instruction_2
);

  Register u_next_instruction (.D(next_instruction), .en(1'b1), .Q(next_instruction_2), .clk(Clock), .clr(Reset));
  Register #(.width(20)) u_Instruction (.D(Instruction), .en(1'b1), .Q(Instruction_2), .clk(Clock), .clr(Reset));
endmodule

module ID_EX (
  input  Clock,
  input  [3:0] RS,
  input  BranchNEq,
  input  BranchEq,
  input  RegDst,
  input  MemWrite,
  input  MemRead,
  input  [3:0] RT,
  input  [3:0] RD,
  input  [7:0] Next_Instruction,
  input  ALU_Src,
  input  Shift,
  input  Reg_Write,
  input  [7:0] Read_data1,
  input  [7:0] Read_data2,
  input  [2:0] Alu_Op,
  input  [3:0] Shift_Amount,
  input  MemToReg,
  input  Reset,
  input  [7:0] Immediate,
  output [3:0] RS_2,
  output BranchNEq_2,
  output BranchEq_2,
  output RegDst_2,
  output MemWrite_2,
  output MemRead_2,
  output [3:0] RT_2,
  output [3:0] RD_2,
  output [7:0] Next_Instruction_2,
  output ALU_Src_2,
  output Shift_2,
  output Reg_Write_2,
  output [7:0] Read_data1_2,
  output [7:0] Read_data2_2,
  output [2:0] Alu_Op_2,
  output [7:0] Shift_Amount_2,
  output MemToReg_2,
  output [7:0] Immediate_2
);

  Register #(.width(4)) u_RS (.D(RS), .en(1'b1), .Q(RS_2), .clk(Clock), .clr(Reset));
  Register #(.width(1)) u_BranchNEq (.D(BranchNEq), .en(1'b1), .Q(BranchNEq_2), .clk(Clock), .clr(Reset));
  Register #(.width(1)) u_BranchEq (.D(BranchEq), .en(1'b1), .Q(BranchEq_2), .clk(Clock), .clr(Reset));
  Register #(.width(1)) u_RegDst (.D(RegDst), .en(1'b1), .Q(RegDst_2), .clk(Clock), .clr(Reset));
  Register #(.width(1)) u_MemWrite (.D(MemWrite), .en(1'b1), .Q(MemWrite_2), .clk(Clock), .clr(Reset));
  Register #(.width(1)) u_MemRead (.D(MemRead), .en(1'b1), .Q(MemRead_2), .clk(Clock), .clr(Reset));
  Register #(.width(4)) u_RT (.D(RT), .en(1'b1), .Q(RT_2), .clk(Clock), .clr(Reset));
  Register #(.width(4)) u_RD (.D(RD), .en(1'b1), .Q(RD_2), .clk(Clock), .clr(Reset));
  Register u_Next_Instruction (.D(Next_Instruction), .en(1'b1), .Q(Next_Instruction_2), .clk(Clock), .clr(Reset));
  Register #(.width(1)) u_ALU_Src (.D(ALU_Src), .en(1'b1), .Q(ALU_Src_2), .clk(Clock), .clr(Reset));
  Register #(.width(1)) u_Shift (.D(Shift), .en(1'b1), .Q(Shift_2), .clk(Clock), .clr(Reset));
  Register #(.width(1)) u_Reg_Write (.D(Reg_Write), .en(1'b1), .Q(Reg_Write_2), .clk(Clock), .clr(Reset));
  Register u_Read_data1 (.D(Read_data1), .en(1'b1), .Q(Read_data1_2), .clk(Clock), .clr(Reset));
  Register u_Read_data2 (.D(Read_data2), .en(1'b1), .Q(Read_data2_2), .clk(Clock), .clr(Reset));
  Register #(.width(3)) u_Alu_op (.D(Alu_Op), .en(1'b1), .Q(Alu_Op_2), .clk(Clock), .clr(Reset));
  Register #(.width(4)) u_Shift_Amount (
    .D(Shift_Amount), .Q(Shift_Amount_2[3:0]), .clk(Clock), .clr(Reset));  // open: en
  Register #(.width(1)) u_MemToReg (.D(MemToReg), .en(1'b1), .Q(MemToReg_2), .clk(Clock), .clr(Reset));
  Register u_Immediate (.D(Immediate), .en(1'b1), .Q(Immediate_2), .clk(Clock), .clr(Reset));

  assign Shift_Amount_2[7:4] = 4'b0000;
endmodule

module EX_MEM (
  input  Clock,
  input  BranchEq,
  input  BranchNeq,
  input  MemToReg,
  input  MemWrite,
  input  MemRead,
  input  [7:0] Next_Instruction,
  input  Zero,
  input  Reg_Write,
  input  [7:0] ALU_Result,
  input  [7:0] Write_Data,
  input  [3:0] Write_Register,
  input  Reset,
  output BranchEq_2,
  output BranchNeq_2,
  output MemToReg_2,
  output MemWrite_2,
  output MemRead_2,
  output [7:0] Next_Instruction_2,
  output Zero_2,
  output Reg_Write_2,
  output [7:0] ALU_Result_2,
  output [7:0] Write_Data_2,
  output [3:0] Write_Register_2
);

  Register #(.width(1)) u_BranchEq (.D(BranchEq), .en(1'b1), .Q(BranchEq_2), .clk(Clock), .clr(Reset));
  Register #(.width(1)) u_BranchNeq (.D(BranchNeq), .en(1'b1), .Q(BranchNeq_2), .clk(Clock), .clr(Reset));
  Register #(.width(1)) u_MemToReg (.D(MemToReg), .en(1'b1), .Q(MemToReg_2), .clk(Clock), .clr(Reset));
  Register #(.width(1)) u_MemWrite (.D(MemWrite), .en(1'b1), .Q(MemWrite_2), .clk(Clock), .clr(Reset));
  Register #(.width(1)) u_MemRead (.D(MemRead), .en(1'b1), .Q(MemRead_2), .clk(Clock), .clr(Reset));
  Register u_Next_Instruction (.D(Next_Instruction), .en(1'b1), .Q(Next_Instruction_2), .clk(Clock), .clr(Reset));
  Register #(.width(1)) u_Zero (.D(Zero), .en(1'b1), .Q(Zero_2), .clk(Clock), .clr(Reset));
  Register #(.width(1)) u_Reg_Write (.D(Reg_Write), .en(1'b1), .Q(Reg_Write_2), .clk(Clock), .clr(Reset));
  Register u_ALU_Result (.D(ALU_Result), .en(1'b1), .Q(ALU_Result_2), .clk(Clock), .clr(Reset));
  Register u_Write_Data (.D(Write_Data), .en(1'b1), .Q(Write_Data_2), .clk(Clock), .clr(Reset));
  Register #(.width(4)) u_Write_Register (
    .D(Write_Register), .en(1'b1), .Q(Write_Register_2), .clk(Clock), .clr(Reset));
endmodule

module MEM_WB (
  input  Clock,
  input  RegWrite,
  input  [3:0] Write_Register,
  input  MemToReg,
  input  [7:0] Read_Data,
  input  Reset,
  input  [7:0] ALU_Result,
  output RegWrite_2,
  output [3:0] Write_Register_2,
  output MemToReg_2,
  output [7:0] Read_Data_2,
  output [7:0] ALU_Result_2
);

  Register #(.width(1)) u_RegWrite (.D(RegWrite), .en(1'b1), .Q(RegWrite_2), .clk(Clock), .clr(Reset));
  Register #(.width(4)) u_Write_Register (
    .D(Write_Register), .en(1'b1), .Q(Write_Register_2), .clk(Clock), .clr(Reset));
  Register #(.width(1)) u_MemToReg (.D(MemToReg), .en(1'b1), .Q(MemToReg_2), .clk(Clock), .clr(Reset));
  Register u_Read_Data (.D(Read_Data), .en(1'b1), .Q(Read_Data_2), .clk(Clock), .clr(Reset));
  Register u_ALU_Result (.D(ALU_Result), .en(1'b1), .Q(ALU_Result_2), .clk(Clock), .clr(Reset));
endmodule

// Forwarding Unit
module Forwarding_Unit (
  input  [3:0] ID_EX_RS,
  input  [3:0] ID_EX_RT,
  input  [3:0] EX_MEM_Reg_RD,
  input  [3:0] MEM_WB_Reg_RD,
  input  MEM_WB_reg_write,
  input  Shift,
  input  EX_MEM_reg_write,
  input  ALU_Src,
  output [1:0] ForwardA,
  output [1:0] ForwardB
);

  wire and_1_out, and_2_out, and_3_out, and_4_out, comparator_1_eq, comparator_2_eq, comparator_3_eq,
       comparator_4_eq, comparator_5_eq, comparator_6_eq, nand_1_out, nand_2_out, not_1_out, not_2_out;
  wire [1:0] or_1_out, or_3_out;

  Comparator #(.width(4)) comparator_1 (.a(ID_EX_RS), .b(EX_MEM_Reg_RD), .eq(comparator_1_eq));  // open: gt, lt
  Comparator #(.width(4)) comparator_2 (.a(EX_MEM_Reg_RD), .b(4'b0110), .eq(comparator_2_eq));  // open: gt, lt
  not not_1 (not_1_out, comparator_2_eq);
  Comparator #(.width(4)) comparator_3 (.a(MEM_WB_Reg_RD), .b(4'b0110), .eq(comparator_3_eq));  // open: gt, lt
  not not_2 (not_2_out, comparator_3_eq);
  Comparator #(.width(4)) comparator_4 (.a(ID_EX_RS), .b(MEM_WB_Reg_RD), .eq(comparator_4_eq));  // open: gt, lt
  Comparator #(.width(4)) comparator_5 (.a(ID_EX_RT), .b(EX_MEM_Reg_RD), .eq(comparator_5_eq));  // open: gt, lt
  Comparator #(.width(4)) comparator_6 (.a(MEM_WB_Reg_RD), .b(ID_EX_RT), .eq(comparator_6_eq));  // open: gt, lt
  nand nand_1 (nand_1_out, not_1_out, comparator_1_eq, EX_MEM_reg_write);
  nand nand_2 (nand_2_out, EX_MEM_reg_write, not_1_out, comparator_5_eq);
  and and_1 (and_1_out, comparator_1_eq, not_1_out, EX_MEM_reg_write);
  and and_2 (and_2_out, comparator_5_eq, not_1_out, EX_MEM_reg_write);
  and and_3 (and_3_out, nand_1_out, not_2_out, MEM_WB_reg_write, comparator_4_eq);
  and and_4 (and_4_out, nand_2_out, MEM_WB_reg_write, not_2_out, comparator_6_eq);
  or or_1 (or_1_out[0], and_1_out, Shift);
  or or_2 (or_1_out[1], and_3_out, Shift);
  or or_3 (or_3_out[0], and_2_out, ALU_Src);
  or or_4 (or_3_out[1], and_4_out, ALU_Src);
  Multiplexer #(.select(2), .width(2), .enable("false")) multiplexer_1 (
    .in0(2'b00), .in1(2'b10), .in2(2'b01), .in3(2'b11), .out(ForwardA), .sel(or_1_out));
  Multiplexer #(.select(2), .width(2), .enable("false")) multiplexer_2 (
    .in0(2'b00), .in1(2'b10), .in2(2'b01), .in3(2'b11), .out(ForwardB), .sel(or_3_out));
endmodule

module Pipelined (
  input  Reset,
  output [7:0] t0,
  output [7:0] t1,
  output [7:0] t2,
  output [7:0] t3,
  output [7:0] t4,
  output [7:0] t5,
  output [7:0] sp
);

  wire Clock_out, control_unit_1_alusrc, control_unit_1_brancheq, control_unit_1_branchneq,
       control_unit_1_memread, control_unit_1_memtoreg, control_unit_1_memwrite, control_unit_1_regdst,
       control_unit_1_regwrite, control_unit_1_shift, ex_mem_1_brancheq_2, ex_mem_1_branchneq_2,
       ex_mem_1_memread_2, ex_mem_1_memtoreg_2, ex_mem_1_memwrite_2, ex_mem_1_reg_write_2, ex_mem_1_zero_2,
       id_ex_1_alu_src_2, id_ex_1_brancheq_2, id_ex_1_branchneq_2, id_ex_1_memread_2, id_ex_1_memtoreg_2,
       id_ex_1_memwrite_2, id_ex_1_reg_write_2, id_ex_1_regdst_2, id_ex_1_shift_2, mem_wb_1_memtoreg_2,
       mem_wb_1_regwrite_2, mips_alu_8_bit_by_tushar_1_p4, multiplexer_5_out;
  wire [1:0] forwarding_unit_1_forwarda, forwarding_unit_1_forwardb;
  wire [2:0] control_unit_1_aluop, id_ex_1_alu_op_2;
  wire [3:0] ex_mem_1_write_register_2, id_ex_1_rd_2, id_ex_1_rs_2, id_ex_1_rt_2, mem_wb_1_write_register_2,
       multiplexer_2_out;
  wire [7:0] adder_1_out, adder_2_out, ex_mem_1_alu_result_2, ex_mem_1_next_instruction_2,
       ex_mem_1_write_data_2, id_ex_1_immediate_2, id_ex_1_next_instruction_2, id_ex_1_read_data1_2,
       id_ex_1_read_data2_2, id_ex_1_shift_amount_2, if_id_1_next_instruction_2, mem_wb_1_alu_result_2,
       mem_wb_1_read_data_2, mips_alu_8_bit_by_tushar_1_p2, mips_alu_8_bit_by_tushar_1_p5, multiplexer_1_out,
       multiplexer_3_out, multiplexer_6_out, PC_q, ram_1_data, register_file_1_read_data_1,
       register_file_1_read_data_2;
  wire [19:0] if_id_1_instruction_2, rom_1_data;

  Multiplexer #(.width(8), .disabled(0), .enable("false")) multiplexer_1 (
    .in0(adder_1_out), .in1(ex_mem_1_next_instruction_2), .out(multiplexer_1_out), .sel(multiplexer_5_out));
  Register PC (.D(multiplexer_1_out), .en(1'b1), .Q(PC_q), .clk(Clock_out), .clr(Reset));
  Clock Clock (.out(Clock_out));
  Adder adder_1 (.a(PC_q), .b(8'h1), .out(adder_1_out));  // open: cin, cout
  ROM #(.dataWidth(20)) rom_1 (.addr(PC_q), .data(rom_1_data));  // open: sel
  IF_ID if_id_1 (
    .next_instruction(adder_1_out), .Clock(Clock_out), .Instruction(rom_1_data),
    .next_instruction_2(if_id_1_next_instruction_2), .Instruction_2(if_id_1_instruction_2), .Reset(Reset));
  // AND_Gate and_1 is placed but not wired
  Control_Unit control_unit_1 (
    .OpCode(if_id_1_instruction_2[19:16]), .RegDst(control_unit_1_regdst), .ALUSrc(control_unit_1_alusrc),
    .MemtoReg(control_unit_1_memtoreg), .MemRead(control_unit_1_memread), .MemWrite(control_unit_1_memwrite),
    .BranchEq(control_unit_1_brancheq), .BranchNeq(control_unit_1_branchneq), .ALUOp(control_unit_1_aluop),
    .RegWrite(control_unit_1_regwrite), .Shift(control_unit_1_shift));  // open: Jump
  Register_File register_file_1 (
    .Write_Data(multiplexer_6_out), .RegWrite(mem_wb_1_regwrite_2),
    .Read_Register_1(if_id_1_instruction_2[15:12]), .Read_Register_2(if_id_1_instruction_2[11:8]),
    .Read_Data_1(register_file_1_read_data_1), .Read_Data_2(register_file_1_read_data_2),
    .Write_Register(mem_wb_1_write_register_2), .R1({t3, t2, t1, t0}), .R2({sp, t5, t4}), .Clock(Clock_out),
    .Reset(Reset));
  ID_EX id_ex_1 (
    .Shift(control_unit_1_shift), .Reg_Write(control_unit_1_regwrite),
    .Read_data1(register_file_1_read_data_1), .Read_data2(register_file_1_read_data_2),
    .Alu_Op(control_unit_1_aluop), .Shift_Amount(if_id_1_instruction_2[3:0]),
    .MemToReg(control_unit_1_memtoreg), .Shift_2(id_ex_1_shift_2), .Reg_Write_2(id_ex_1_reg_write_2),
    .Read_data1_2(id_ex_1_read_data1_2), .Read_data2_2(id_ex_1_read_data2_2), .Alu_Op_2(id_ex_1_alu_op_2),
    .Shift_Amount_2(id_ex_1_shift_amount_2), .MemToReg_2(id_ex_1_memtoreg_2), .Reset(Reset),
    .Clock(Clock_out), .Immediate(if_id_1_instruction_2[7:0]), .Immediate_2(id_ex_1_immediate_2),
    .ALU_Src(control_unit_1_alusrc), .ALU_Src_2(id_ex_1_alu_src_2),
    .Next_Instruction(if_id_1_next_instruction_2), .Next_Instruction_2(id_ex_1_next_instruction_2),
    .RD(if_id_1_instruction_2[7:4]), .RD_2(id_ex_1_rd_2), .RT(if_id_1_instruction_2[11:8]),
    .RT_2(id_ex_1_rt_2), .MemRead(control_unit_1_memread), .MemRead_2(id_ex_1_memread_2),
    .MemWrite(control_unit_1_memwrite), .MemWrite_2(id_ex_1_memwrite_2), .RegDst(control_unit_1_regdst),
    .RegDst_2(id_ex_1_regdst_2), .BranchEq(control_unit_1_brancheq), .BranchEq_2(id_ex_1_brancheq_2),
    .BranchNEq(control_unit_1_branchneq), .BranchNEq_2(id_ex_1_branchneq_2),
    .RS(if_id_1_instruction_2[15:12]), .RS_2(id_ex_1_rs_2));
  Multiplexer #(.width(4), .disabled(0), .enable("false")) multiplexer_2 (
    .in0(id_ex_1_rt_2), .in1(id_ex_1_rd_2), .out(multiplexer_2_out), .sel(id_ex_1_regdst_2));
  Forwarding_Unit forwarding_unit_1 (
    .ID_EX_RS(id_ex_1_rs_2), .ID_EX_RT(id_ex_1_rt_2), .EX_MEM_Reg_RD(ex_mem_1_write_register_2),
    .MEM_WB_Reg_RD(mem_wb_1_write_register_2), .MEM_WB_reg_write(mem_wb_1_regwrite_2),
    .EX_MEM_reg_write(ex_mem_1_reg_write_2), .ForwardA(forwarding_unit_1_forwarda),
    .ForwardB(forwarding_unit_1_forwardb), .Shift(id_ex_1_shift_2), .ALU_Src(id_ex_1_alu_src_2));
  Adder adder_2 (.a(id_ex_1_next_instruction_2), .b(id_ex_1_immediate_2), .out(adder_2_out));  // open: cin, cout
  Multiplexer #(.select(2), .width(8), .disabled(0), .enable("false")) multiplexer_3 (
    .in0(id_ex_1_read_data1_2), .in1(multiplexer_6_out), .in2(ex_mem_1_alu_result_2),
    .in3(id_ex_1_shift_amount_2), .out(multiplexer_3_out), .sel(forwarding_unit_1_forwarda));
  // MIPS_ALU_8_bit_by_Tushar mips_alu_8_bit_by_tushar_1: pin names not known; wires that end beside it: multiplexer_3_out, mips_alu_8_bit_by_tushar_1_p2, id_ex_1_alu_op_2, mips_alu_8_bit_by_tushar_1_p4, mips_alu_8_bit_by_tushar_1_p5
  Multiplexer #(.select(2), .width(8), .disabled(0), .enable("false")) multiplexer_4 (
    .in0(id_ex_1_read_data2_2), .in1(multiplexer_6_out), .in2(ex_mem_1_alu_result_2),
    .in3(id_ex_1_immediate_2), .out(mips_alu_8_bit_by_tushar_1_p2), .sel(forwarding_unit_1_forwardb));
  EX_MEM ex_mem_1 (
    .Reg_Write(id_ex_1_reg_write_2), .ALU_Result(mips_alu_8_bit_by_tushar_1_p5),
    .Write_Data(id_ex_1_read_data2_2), .Reg_Write_2(ex_mem_1_reg_write_2),
    .ALU_Result_2(ex_mem_1_alu_result_2), .Write_Data_2(ex_mem_1_write_data_2), .Clock(Clock_out),
    .Reset(Reset), .Zero(mips_alu_8_bit_by_tushar_1_p4), .Zero_2(ex_mem_1_zero_2),
    .Next_Instruction(adder_2_out), .Next_Instruction_2(ex_mem_1_next_instruction_2),
    .Write_Register(multiplexer_2_out), .Write_Register_2(ex_mem_1_write_register_2),
    .MemRead(id_ex_1_memread_2), .MemRead_2(ex_mem_1_memread_2), .MemWrite(id_ex_1_memwrite_2),
    .MemWrite_2(ex_mem_1_memwrite_2), .MemToReg(id_ex_1_memtoreg_2), .MemToReg_2(ex_mem_1_memtoreg_2),
    .BranchNeq(id_ex_1_branchneq_2), .BranchNeq_2(ex_mem_1_branchneq_2), .BranchEq(id_ex_1_brancheq_2),
    .BranchEq_2(ex_mem_1_brancheq_2));
  Multiplexer #(.disabled(0), .enable("false")) multiplexer_5 (
    .in0(ex_mem_1_branchneq_2), .in1(ex_mem_1_brancheq_2), .out(multiplexer_5_out), .sel(ex_mem_1_zero_2));
  RAM #(.bus("separate")) ram_1 (
    .addr(ex_mem_1_alu_result_2), .din(ex_mem_1_write_data_2), .data(ram_1_data), .str(ex_mem_1_memwrite_2),
    .sel(1'b1), .clk(Clock_out), .ld(ex_mem_1_memread_2), .clr(Reset));
  MEM_WB mem_wb_1 (
    .MemToReg(ex_mem_1_memtoreg_2), .Read_Data(ram_1_data), .ALU_Result(ex_mem_1_alu_result_2),
    .MemToReg_2(mem_wb_1_memtoreg_2), .Read_Data_2(mem_wb_1_read_data_2),
    .ALU_Result_2(mem_wb_1_alu_result_2), .Reset(Reset), .Write_Register(ex_mem_1_write_register_2),
    .Write_Register_2(mem_wb_1_write_register_2), .RegWrite(ex_mem_1_reg_write_2),
    .RegWrite_2(mem_wb_1_regwrite_2), .Clock(Clock_out));
  Multiplexer #(.width(8), .enable("false")) multiplexer_6 (
    .in0(mem_wb_1_alu_result_2), .in1(mem_wb_1_read_data_2), .out(multiplexer_6_out),
    .sel(mem_wb_1_memtoreg_2));
  // AND_Gate and_2 is placed but not wired

  // Notes on the sheet:
  //   Instruction Memory
  //   contents of rom_1 (hex, n*v repeats v):
  //   167ff 16001 16102 16203 16304 16405 4*16000 62310 e1240 1340 64340
  //   Register Values
  //   Data Memory
endmodule
