// Logisim project test.circ as structural Verilog: 1 circuit, main circuit main
module main (
  input  A0,
  input  A1,
  input  A2,
  input  A3,
  input  B0,
  input  B1,
  input  B2,
  input  B3,
  input  S0,
  input  S1,
  input  S3
);

  wire adder_1_cout, decoder_1_out1, decoder_1_out2, decoder_1_out3, decoder_1_out5, decoder_1_out6,
       decoder_1_out7, or_1_out, or_2_out, or_3_out, or_4_out, or_5_out, xor_5_out, xor_6_out, xor_7_out,
       xor_8_out;
  wire [3:0] adder_1_out, multiplexer_1_out, xor_1_out;

  Decoder #(.enable("false"), .select(3)) decoder_1 (
    .out1(decoder_1_out1), .out2(decoder_1_out2), .out3(decoder_1_out3), .out5(decoder_1_out5),
    .out6(decoder_1_out6), .out7(decoder_1_out7), .sel({S3, S1, S0}));  // open: out0, out4
  or or_1 (or_1_out, decoder_1_out2, decoder_1_out3);
  or or_2 (or_2_out, decoder_1_out6, decoder_1_out7);
  or or_3 (or_3_out, decoder_1_out1, decoder_1_out2);
  or or_4 (or_4_out, decoder_1_out3, decoder_1_out5);
  or or_5 (or_5_out, or_3_out, or_4_out);
  xor xor_1 (xor_1_out[0], A0, or_1_out);
  xor xor_2 (xor_1_out[1], A1, or_1_out);
  xor xor_3 (xor_1_out[2], A2, or_1_out);
  xor xor_4 (xor_1_out[3], A3, or_1_out);
  xor xor_5 (xor_5_out, B0, or_2_out);
  xor xor_6 (xor_6_out, B1, or_2_out);
  xor xor_7 (xor_7_out, B2, or_2_out);
  xor xor_8 (xor_8_out, B3, or_2_out);
  Multiplexer multiplexer_1 (.in0(xor_5_out), .in1(1'b0), .out(multiplexer_1_out[0]), .sel(or_5_out));
  Multiplexer multiplexer_2 (.in0(xor_6_out), .in1(1'b0), .out(multiplexer_1_out[1]), .sel(or_5_out));
  Multiplexer multiplexer_3 (.in0(xor_7_out), .in1(1'b0), .out(multiplexer_1_out[2]), .sel(or_5_out));
  Multiplexer multiplexer_4 (.in0(xor_8_out), .in1(1'b0), .out(multiplexer_1_out[3]), .sel(or_5_out));
  Adder #(.width(4)) adder_1 (
    .a(xor_1_out), .b(multiplexer_1_out), .out(adder_1_out), .cin(decoder_1_out5), .cout(adder_1_cout));
endmodule
