// Logisim project A2_Group5_v2.circ as structural Verilog: 12 circuits, main circuit main
module main (
  input  [31:0] Number_A,
  input  [31:0] Number_B,
  output [31:0] Output,
  output Overflow,
  output Underflow
);

  wire multiplexer_1_out, multiplexer_2_out, n12_bit_comparator_1_exp_a___exp_b,
       normalizer_1_significand_contains_one, overflow_underflow_setter_1_overflow,
       rounding_circuit_1_overflow;
  wire [4:0] n12_to_5_bit_shrinker_1__5_bit_lsb_output;
  wire [11:0] multiplexer_3_out, n12_bit_comparator_1_difference_of_exp, normalizer_1_exponent_output;
  wire [31:0] multiplexer_4_out, multiplexer_5_out, n19_to_32_bit_padder_1__32_bit_padded_significand,
       n19_to_32_bit_padder_2__32_bit_padded_significand, n32_bit_adder_1__32_bit_significand,
       normalizer_1_significand_output, rounding_circuit_1_significand_2, shifter_1_out;

  Multiplexer #(.enable("false")) multiplexer_1 (
    .in0(Number_B[31]), .in1(Number_A[31]), .out(multiplexer_1_out), .sel(n12_bit_comparator_1_exp_a___exp_b));
  Multiplexer #(.enable("false")) multiplexer_2 (
    .in0(Number_A[31]), .in1(Number_B[31]), .out(multiplexer_2_out), .sel(n12_bit_comparator_1_exp_a___exp_b));
  _19_to_32_bit_padder u_19_to_32_bit_padder_1 (
    ._31_bit_input(Number_A[30:0]),
    ._32_bit_padded_significand(n19_to_32_bit_padder_1__32_bit_padded_significand));
  Multiplexer #(.width(12), .enable("false")) multiplexer_3 (
    .in0(Number_B[30:19]), .in1(Number_A[30:19]), .out(multiplexer_3_out),
    .sel(n12_bit_comparator_1_exp_a___exp_b));
  rounding_circuit rounding_circuit_1 (
    .Significand(normalizer_1_significand_output), .Exponent(normalizer_1_exponent_output),
    .significand_2({rounding_circuit_1_significand_2[31:30], Output[18:0], rounding_circuit_1_significand_2[10:0]}),
    .Exponent_2(Output[30:19]), .Overflow(rounding_circuit_1_overflow));
  _32_Bit_adder u_32_bit_adder_1 (
    .Significand_1(shifter_1_out), .Significand_2(multiplexer_4_out), .Lower_num_sign(multiplexer_2_out),
    .Higher_num_sign(multiplexer_1_out), ._32_bit_significand(n32_bit_adder_1__32_bit_significand),
    .sign_bit(Output[31]));
  Normalizer normalizer_1 (
    .Exponent(multiplexer_3_out), .Significand(n32_bit_adder_1__32_bit_significand),
    .Exponent_Output(normalizer_1_exponent_output), .Significand_output(normalizer_1_significand_output),
    .Significand_contains_one(normalizer_1_significand_contains_one));
  _12_Bit_comparator u_12_bit_comparator_1 (
    .Exponent_B(Number_B[30:19]), .Exponent_A(Number_A[30:19]),
    .Difference_of_Exp(n12_bit_comparator_1_difference_of_exp),
    .Exp_A___Exp_B(n12_bit_comparator_1_exp_a___exp_b));
  overflow_underflow_setter overflow_underflow_setter_1 (
    .Exponent(normalizer_1_exponent_output),
    .All_bits_of_significant_are_not_zero(normalizer_1_significand_contains_one),
    .Overflow(overflow_underflow_setter_1_overflow), .Underflow(Underflow));
  or or_1 (Overflow, rounding_circuit_1_overflow, overflow_underflow_setter_1_overflow);
  _19_to_32_bit_padder u_19_to_32_bit_padder_2 (
    ._31_bit_input(Number_B[30:0]),
    ._32_bit_padded_significand(n19_to_32_bit_padder_2__32_bit_padded_significand));
  Multiplexer #(.width(32), .enable("false")) multiplexer_4 (
    .in0(n19_to_32_bit_padder_2__32_bit_padded_significand),
    .in1(n19_to_32_bit_padder_1__32_bit_padded_significand), .out(multiplexer_4_out),
    .sel(n12_bit_comparator_1_exp_a___exp_b));
  _12_to_5_Bit_Shrinker u_12_to_5_bit_shrinker_1 (
    ._12_bit_input(n12_bit_comparator_1_difference_of_exp),
    ._5_bit_lsb_output(n12_to_5_bit_shrinker_1__5_bit_lsb_output));
  Multiplexer #(.width(32), .enable("false")) multiplexer_5 (
    .in0(n19_to_32_bit_padder_1__32_bit_padded_significand),
    .in1(n19_to_32_bit_padder_2__32_bit_padded_significand), .out(multiplexer_5_out),
    .sel(n12_bit_comparator_1_exp_a___exp_b));
  Shifter #(.width(32), .shift("lr")) shifter_1 (
    .in(multiplexer_5_out), .\dist (n12_to_5_bit_shrinker_1__5_bit_lsb_output), .out(shifter_1_out));

  // Notes on the sheet:
  //   32 bit padder
  //   1 bit sign, 12 bit exponent, 19 bit fraction
  //   32 bit adder
  //   Normalizer
  //   Rounder
  //   taking exact 19 bit
  //   Compare 12 bit
  //   overflow underflow setter
  //   12 to 5 bit shrinker
  //   32 bit padder
  //   32 bit right shift
endmodule

module _32_Bit_adder (
  input  [31:0] Significand_1,
  input  [31:0] Significand_2,
  input  Lower_num_sign,
  input  Higher_num_sign,
  output [31:0] _32_bit_significand,
  output sign_bit
);

  wire comparator_1_lt, xor_1_out;
  wire [31:0] multiplexer_1_out, multiplexer_2_out, multiplexer_4_out, negator_1_out;

  Comparator #(.width(32)) comparator_1 (.a(Significand_1), .b(Significand_2), .lt(comparator_1_lt));  // open: gt, eq
  Multiplexer #(.width(32), .enable("false")) multiplexer_1 (
    .in0(Significand_2), .in1(Significand_1), .out(multiplexer_1_out), .sel(comparator_1_lt));
  Multiplexer #(.width(32), .enable("false")) multiplexer_2 (
    .in0(Significand_1), .in1(Significand_2), .out(multiplexer_2_out), .sel(comparator_1_lt));
  xor xor_1 (xor_1_out, Lower_num_sign, Higher_num_sign);
  Negator #(.width(32)) negator_1 (.in(multiplexer_1_out), .out(negator_1_out));
  Multiplexer #(.enable("false")) multiplexer_3 (
    .in0(Lower_num_sign), .in1(Higher_num_sign), .out(sign_bit), .sel(comparator_1_lt));
  Multiplexer #(.width(32), .enable("false")) multiplexer_4 (
    .in0(multiplexer_1_out), .in1(negator_1_out), .out(multiplexer_4_out), .sel(xor_1_out));
  Adder #(.width(32)) adder_1 (
    .a(multiplexer_4_out), .b(multiplexer_2_out), .out(_32_bit_significand));  // open: cin, cout

  // Notes on the sheet:
  //   Compares if 1 < 2
  //   32 bit negator
endmodule

module _12_Bit_comparator (
  input  [11:0] Exponent_B,
  input  [11:0] Exponent_A,
  output [11:0] Difference_of_Exp,
  output Exp_A___Exp_B
);

  wire [11:0] negator_1_out, subtractor_1_out;

  Subtractor #(.width(12)) subtractor_1 (
    .a(Exponent_B), .b(Exponent_A), .out(subtractor_1_out), .bin(1'b0), .bout(Exp_A___Exp_B));
  Negator #(.width(12)) negator_1 (.in(subtractor_1_out), .out(negator_1_out));
  Multiplexer #(.width(12), .enable("false")) multiplexer_1 (
    .in0(subtractor_1_out), .in1(negator_1_out), .out(Difference_of_Exp), .sel(Exp_A___Exp_B));

  // Notes on the sheet:
  //   12 bit subtractor
  //   12 bit negator
endmodule

module Normalizer (
  input  [11:0] Exponent,
  input  [31:0] Significand,
  output Significand_contains_one,
  output [31:0] Significand_output,
  output [11:0] Exponent_Output
);

  wire and_1_out, and_2_out, and_3_out, and_4_out, nor_1_out, or_1_out, subtractor_1_bout, xor_1_out;
  wire [4:0] n12_to_5_bit_shrinker_1__5_bit_lsb_output, set_bit_finder_1_shift_amount;
  wire [11:0] multiplexer_1_out, multiplexer_3_out, multiplexer_4_out, n5_to_12_bit_padder_1__12_bit_output,
       subtractor_1_out, subtractor_2_out;
  wire [31:0] shifter_1_out;

  and and_1 (and_1_out, Exponent[11], Exponent[10], Exponent[9], Exponent[8], Exponent[7], Exponent[6], Exponent[5], Exponent[4], Exponent[3], Exponent[2], Exponent[1], Exponent[0]);
  Subtractor #(.width(12)) subtractor_1 (
    .a(Exponent), .b(multiplexer_3_out), .out(subtractor_1_out), .bin(1'b0), .bout(subtractor_1_bout));
  Multiplexer #(.width(12), .enable("false")) multiplexer_1 (
    .in0(subtractor_1_out), .in1({12{1'b0}}), .out(multiplexer_1_out), .sel(and_3_out));
  Multiplexer #(.width(12), .enable("false")) multiplexer_2 (
    .in0(multiplexer_1_out), .in1({12{1'b1}}), .out(Exponent_Output), .sel(and_1_out));
  Multiplexer #(.width(12), .enable("false")) multiplexer_3 (
    .in0(n5_to_12_bit_padder_1__12_bit_output), .in1({12{1'b1}}), .out(multiplexer_3_out), .sel(and_4_out));
  xor xor_1 (xor_1_out, Significand[31], 1'b1);
  nor nor_1 (nor_1_out, subtractor_1_out[0], subtractor_1_out[1], subtractor_1_out[2], subtractor_1_out[3], subtractor_1_out[4], subtractor_1_out[5], subtractor_1_out[6], subtractor_1_out[7], subtractor_1_out[8], subtractor_1_out[9], subtractor_1_out[10], subtractor_1_out[11]);
  Subtractor #(.width(12)) subtractor_2 (
    .a(Exponent), .b({12{1'b0}}), .out(subtractor_2_out), .bin(nor_1_out));  // open: bout
  or or_1 (or_1_out, subtractor_1_bout, nor_1_out);
  and and_2 (and_2_out, Exponent_Output[0], Exponent_Output[1], Exponent_Output[2], Exponent_Output[3], Exponent_Output[4], Exponent_Output[5], Exponent_Output[6], Exponent_Output[7], Exponent_Output[8], Exponent_Output[9], Exponent_Output[10], Exponent_Output[11]);
  and and_3 (and_3_out, xor_1_out, or_1_out);
  Multiplexer #(.width(12), .enable("false")) multiplexer_4 (
    .in0(n5_to_12_bit_padder_1__12_bit_output), .in1(subtractor_2_out), .out(multiplexer_4_out),
    .sel(and_3_out));
  Set_bit_finder set_bit_finder_1 (
    ._32_bit_input(Significand), .Shift_amount(set_bit_finder_1_shift_amount),
    .contains_one(Significand_contains_one));
  _5_to_12_Bit_padder u_5_to_12_bit_padder_1 (
    ._5_bit_input(set_bit_finder_1_shift_amount), ._12_bit_output(n5_to_12_bit_padder_1__12_bit_output));
  _12_to_5_Bit_Shrinker u_12_to_5_bit_shrinker_1 (
    ._12_bit_input(multiplexer_4_out), ._5_bit_lsb_output(n12_to_5_bit_shrinker_1__5_bit_lsb_output));
  Shifter #(.width(32), .shift("rl")) shifter_1 (
    .in(Significand), .\dist (n12_to_5_bit_shrinker_1__5_bit_lsb_output), .out(shifter_1_out));
  and and_4 (and_4_out, set_bit_finder_1_shift_amount[4], set_bit_finder_1_shift_amount[3], set_bit_finder_1_shift_amount[2], set_bit_finder_1_shift_amount[1], set_bit_finder_1_shift_amount[0]);
  Multiplexer #(.width(32), .enable("false")) multiplexer_5 (
    .in0({1'b0, shifter_1_out[30:0]}), .in1(32'h40000000), .out(Significand_output), .sel(and_2_out));

  // Notes on the sheet:
  //   12 bit subtractor
  //   12 bit subtractor
  //   12 to 5 bit shrinker
  //   Set bit finder, finds place and existence of first one
  //   12 bit padder
  //   32 bit left rotator
endmodule

module _19_to_32_bit_padder (
  input  [30:0] _31_bit_input,
  output [31:0] _32_bit_padded_significand
);

  or Or___11 (_32_bit_padded_significand[30], _31_bit_input[19], _31_bit_input[20], _31_bit_input[21], _31_bit_input[22], _31_bit_input[23], _31_bit_input[24], _31_bit_input[25], _31_bit_input[26], _31_bit_input[27], _31_bit_input[28], _31_bit_input[29], _31_bit_input[30]);

  assign {_32_bit_padded_significand[31], _32_bit_padded_significand[29:0]} = {1'b0, _31_bit_input[18:0], {11{1'b0}}};

  // Notes on the sheet:
  //   this or checks if exp non zero
endmodule

module _5_to_12_Bit_padder (
  input  [4:0] _5_bit_input,
  output [11:0] _12_bit_output
);


  assign _12_bit_output = {{7{1'b0}}, _5_bit_input};
endmodule

module Set_bit_finder (
  input  [31:0] _32_bit_input,
  output [4:0] Shift_amount,
  output contains_one
);

  wire [4:0] bitfinder_1_index;

  BitFinder #(.width(32)) bitfinder_1 (
    .in({_32_bit_input[0], _32_bit_input[1], _32_bit_input[2], _32_bit_input[3], _32_bit_input[4], _32_bit_input[5], _32_bit_input[6], _32_bit_input[7], _32_bit_input[8], _32_bit_input[9], _32_bit_input[10], _32_bit_input[11], _32_bit_input[12], _32_bit_input[13], _32_bit_input[14], _32_bit_input[15], _32_bit_input[16], _32_bit_input[17], _32_bit_input[18], _32_bit_input[19], _32_bit_input[20], _32_bit_input[21], _32_bit_input[22], _32_bit_input[23], _32_bit_input[24], _32_bit_input[25], _32_bit_input[26], _32_bit_input[27], _32_bit_input[28], _32_bit_input[29], _32_bit_input[30], _32_bit_input[31]}),
    .index(bitfinder_1_index), .found(contains_one));
  Subtractor #(.width(5)) subtractor_1 (
    .a(bitfinder_1_index), .b({5{1'b0}}), .out(Shift_amount), .bin(1'b1));  // open: bout

  // Notes on the sheet:
  //   bit finder, finds indx of input's lowest order 1
  //   5 bit subtractor
endmodule

module overflow_underflow_setter (
  input  [11:0] Exponent,
  input  All_bits_of_significant_are_not_zero,
  output Overflow,
  output Underflow
);

  wire nor_1_out;

  nor nor_1 (nor_1_out, Exponent[0], Exponent[1], Exponent[2], Exponent[3], Exponent[4], Exponent[5], Exponent[6], Exponent[7], Exponent[8], Exponent[9], Exponent[10], Exponent[11]);
  and and_1 (Overflow, Exponent[0], Exponent[1], Exponent[2], Exponent[3], Exponent[4], Exponent[5], Exponent[6], Exponent[7], Exponent[8], Exponent[9], Exponent[10], Exponent[11]);
  and and_2 (Underflow, nor_1_out, All_bits_of_significant_are_not_zero);
endmodule

module rounding_circuit (
  input  [31:0] Significand,
  input  [11:0] Exponent,
  output [31:0] significand_2,
  output [11:0] Exponent_2,
  output Overflow
);

  wire [31:0] rounding_mini_1__32_bit_significand_output;

  rounding_mini rounding_mini_1 (
    ._32_bit_Significand(Significand), ._32_bit_Significand_Output(rounding_mini_1__32_bit_significand_output));
  Adder #(.width(12)) adder_1 (
    .a(Exponent), .b({12{1'b0}}), .out(Exponent_2), .cin(rounding_mini_1__32_bit_significand_output[31]));  // open: cout
  Shifter #(.width(32), .shift("lr")) shifter_1 (
    .in(rounding_mini_1__32_bit_significand_output),
    .\dist ({4'b0000, rounding_mini_1__32_bit_significand_output[31]}), .out(significand_2));
  and and_1 (Overflow, Exponent_2[0], Exponent_2[1], Exponent_2[2], Exponent_2[3], Exponent_2[4], Exponent_2[5], Exponent_2[6], Exponent_2[7], Exponent_2[8], Exponent_2[9], Exponent_2[10], Exponent_2[11]);

  // Notes on the sheet:
  //   12 bit adder
  //   32 bit right shift
endmodule

module rounding_mini (
  input  [31:0] _32_bit_Significand,
  output [31:0] _32_bit_Significand_Output
);

  wire or_1_out, OR_for_S_out;
  wire [11:11] and_1_out;

  or OR_for_S (OR_for_S_out, _32_bit_Significand[0], _32_bit_Significand[1], _32_bit_Significand[2], _32_bit_Significand[3], _32_bit_Significand[4], _32_bit_Significand[5], _32_bit_Significand[6], _32_bit_Significand[7], _32_bit_Significand[8]);
  or or_1 (or_1_out, OR_for_S_out, _32_bit_Significand[11], _32_bit_Significand[9]);
  and and_1 (and_1_out[11], or_1_out, _32_bit_Significand[10]);
  Adder #(.width(32)) adder_1 (
    .a({{20{1'b0}}, and_1_out[11], {11{1'b0}}}), .b(_32_bit_Significand), .out(_32_bit_Significand_Output),
    .cin(1'b0));  // open: cout

  // Notes on the sheet:
  //   S
  //   L
  //   R + L + S
  //   R
  //   G (L+R+S)
  //   G
endmodule

module _12_to_5_Bit_Shrinker (
  input  [11:0] _12_bit_input,
  output [4:0] _5_bit_lsb_output
);

  wire or_1_out;

  or or_1 (or_1_out, _12_bit_input[5], _12_bit_input[6], _12_bit_input[7], _12_bit_input[8], _12_bit_input[9], _12_bit_input[10], _12_bit_input[11]);
  Multiplexer #(.width(5), .enable("false")) multiplexer_1 (
    .in0(_12_bit_input[4:0]), .in1({5{1'b1}}), .out(_5_bit_lsb_output), .sel(or_1_out));
endmodule

module FPA (
  input  [31:0] Number_A,
  input  [31:0] Number_B,
  output Underflow,
  output Overflow,
  output [31:0] Output
);

  main main_1 (.Number_A(Number_A), .Number_B(Number_B), .Output(Output), .Overflow(Overflow), .Underflow(Underflow));

  // Notes on the sheet:
  //   FPA
endmodule
