// Logisim project main_siam.circ as structural Verilog
module main (
  input  in_1,
  output [3:0] t0,
  output [3:0] t1,
  output [3:0] t2,
  output [3:0] t3,
  output [3:0] t4,
  output [3:0] sp
);

  wire alu_1_zero_flag, clock_1_out, control_unit_1_alusrc, control_unit_1_beq, control_unit_1_bneq,
       control_unit_1_jump, control_unit_1_memread, control_unit_1_memtoreg, control_unit_1_memwrite,
       control_unit_1_regdst, control_unit_1_regwrite, multiplexer_4_out;
  wire [2:0] control_unit_1_aluop;
  wire [3:0] alu_1_output, data_memory_1_data_read,
       instruction_memory_1_destination_register_shamt_addr__immediate, instruction_memory_1_opcode,
       instruction_memory_1_source_register_1, instruction_memory_1_source_register_2, multiplexer_1_out,
       multiplexer_5_out, multiplexer_6_out, registers_1_read_data_1, registers_1_read_data_2;
  wire [7:0] adder_1_out, adder_2_out, bit_extender_1_out, instruction_memory_1_pc_read,
       instruction_memory_1_target_jump_address, multiplexer_2_out, multiplexer_3_out;

  // Probe on multiplexer_3_out
  Clock clock_1 (.out(clock_1_out));
  // Probe on instruction_memory_1_pc_read
  Adder adder_1 (.a(instruction_memory_1_pc_read), .b(8'h1), .out(adder_1_out));  // open: cin, cout
  Instruction_Memory instruction_memory_1 (
    .PC_Write(multiplexer_3_out), .CLK(clock_1_out), .Reset(in_1), .PC_read(instruction_memory_1_pc_read),
    .Destination_Register_Shamt_Addr__Immediate(instruction_memory_1_destination_register_shamt_addr__immediate),
    .Source_Register_2(instruction_memory_1_source_register_2),
    .Source_Register_1(instruction_memory_1_source_register_1), .Opcode(instruction_memory_1_opcode),
    .Target_Jump_Address(instruction_memory_1_target_jump_address));
  assign bit_extender_1_out = {{4{instruction_memory_1_destination_register_shamt_addr__immediate[3]}}, instruction_memory_1_destination_register_shamt_addr__immediate};  // Bit_Extender bit_extender_1
  Control_Unit control_unit_1 (
    .OP_Code(instruction_memory_1_opcode), .ALUOp(control_unit_1_aluop), .Jump(control_unit_1_jump),
    .bneq(control_unit_1_bneq), .beq(control_unit_1_beq), .MemWrite(control_unit_1_memwrite),
    .MemRead(control_unit_1_memread), .RegWrite(control_unit_1_regwrite), .MemToReg(control_unit_1_memtoreg),
    .ALUSrc(control_unit_1_alusrc), .RegDst(control_unit_1_regdst));
  Adder adder_2 (.a(bit_extender_1_out), .b(adder_1_out), .out(adder_2_out));  // open: cin, cout
  Multiplexer #(.width(4), .enable("false")) multiplexer_1 (
    .in0(instruction_memory_1_source_register_2),
    .in1(instruction_memory_1_destination_register_shamt_addr__immediate), .out(multiplexer_1_out),
    .sel(control_unit_1_regdst));
  Multiplexer #(.width(8), .enable("false")) multiplexer_2 (
    .in0(adder_1_out), .in1(adder_2_out), .out(multiplexer_2_out), .sel(multiplexer_4_out));
  Registers registers_1 (
    .Dst_Reg_1(multiplexer_1_out), .Write_Data(multiplexer_6_out), .CLR(in_1),
    .Src_Reg_1(instruction_memory_1_source_register_1), .SrcReg2(instruction_memory_1_source_register_2),
    .RegWrite(control_unit_1_regwrite), .CLK(clock_1_out), .t4__t3__t2__t1__t0__sp({sp, t4, t3, t2, t1, t0}),
    .Read_Data_1(registers_1_read_data_1), .Read_Data_2(registers_1_read_data_2));
  Multiplexer #(.width(8), .enable("false")) multiplexer_3 (
    .in0(multiplexer_2_out), .in1(instruction_memory_1_target_jump_address), .out(multiplexer_3_out),
    .sel(control_unit_1_jump));
  Multiplexer #(.enable("false")) multiplexer_4 (
    .in0(control_unit_1_bneq), .in1(control_unit_1_beq), .out(multiplexer_4_out), .sel(alu_1_zero_flag));
  Multiplexer #(.width(4), .enable("false")) multiplexer_5 (
    .in0(registers_1_read_data_2), .in1(instruction_memory_1_destination_register_shamt_addr__immediate),
    .out(multiplexer_5_out), .sel(control_unit_1_alusrc));
  ALU alu_1 (
    .Input_1(registers_1_read_data_1), .Input_2(multiplexer_5_out), .ALU_op_detector(control_unit_1_aluop),
    .Output(alu_1_output), .Zero_flag(alu_1_zero_flag));
  Data_Memory data_memory_1 (
    .Address(alu_1_output), .Write_Data(registers_1_read_data_2), .CLK(clock_1_out), .CLR(in_1),
    .Data_Read(data_memory_1_data_read), .MemRead(control_unit_1_memread), .MemWrite(control_unit_1_memwrite));
  Multiplexer #(.width(4), .enable("false")) multiplexer_6 (
    .in0(alu_1_output), .in1(data_memory_1_data_read), .out(multiplexer_6_out), .sel(control_unit_1_memtoreg));

  // Notes on the sheet:
  //   RegDst Mux
  //   ALUSrc Mux
  //   MemToReg mux
endmodule

module ALU (
  input  [2:0] ALU_op_detector,
  input  [3:0] Input_1,
  input  [3:0] Input_2,
  output [3:0] Output,
  output Zero_flag
);

  wire [3:0] adder_1_out, and_1_out, nor_1_out, or_1_out, shifter_1_out, shifter_2_out, subtractor_1_out;

  Adder #(.width(4)) adder_1 (.a(Input_1), .b(Input_2), .out(adder_1_out), .cin(1'b0));  // open: cout
  Subtractor #(.width(4)) subtractor_1 (.a(Input_1), .b(Input_2), .out(subtractor_1_out), .bin(1'b0));  // open: bout
  assign and_1_out = Input_1 & Input_2;  // AND_Gate and_1, 4 bits wide
  assign or_1_out = Input_1 | Input_2;  // OR_Gate or_1, 4 bits wide
  Shifter #(.width(4), .shift("lr")) shifter_1 (.in(Input_1), .\dist (Input_2[1:0]), .out(shifter_1_out));
  assign nor_1_out = ~(Input_1 | Input_2);  // NOR_Gate nor_1, 4 bits wide
  Shifter #(.width(4)) shifter_2 (.in(Input_1), .\dist (Input_2[1:0]), .out(shifter_2_out));
  Multiplexer #(.select(3), .width(4), .enable("false")) multiplexer_1 (
    .in0(adder_1_out), .in1(subtractor_1_out), .in2(and_1_out), .in3(or_1_out), .in4(nor_1_out),
    .in5(shifter_2_out), .in6(shifter_1_out), .in7(4'b0000), .out(Output), .sel(ALU_op_detector));
  nor nor_2 (Zero_flag, Output[0], Output[1], Output[2], Output[3]);
endmodule

module Instruction_Memory (
  input  [7:0] PC_Write,
  input  CLK,
  input  Reset,
  output [7:0] PC_read,
  output [3:0] Destination_Register_Shamt_Addr__Immediate,
  output [3:0] Source_Register_2,
  output [3:0] Source_Register_1,
  output [3:0] Opcode,
  output [7:0] Target_Jump_Address
);

  Register #(.trigger("falling")) register_1 (.D(PC_Write), .Q(PC_read), .clk(CLK), .clr(Reset));  // open: en
  ROM #(.dataWidth(16)) rom_1 (
    .addr(PC_read),
    .data({Opcode, Source_Register_1, Source_Register_2, Destination_Register_Shamt_Addr__Immediate}),
    .sel(1'b1));

  assign Target_Jump_Address = {Source_Register_1, Source_Register_2};

  // Notes on the sheet:
  //   contents of rom_1 (hex, n*v repeats v):
  //   306f 3074 3015 f17d 3014 f17b
endmodule

module Registers (
  input  RegWrite,
  input  CLK,
  input  [3:0] Dst_Reg_1,
  input  [3:0] Write_Data,
  input  CLR,
  input  [3:0] Src_Reg_1,
  input  [3:0] SrcReg2,
  output [23:0] t4__t3__t2__t1__t0__sp,
  output [3:0] Read_Data_2,
  output [3:0] Read_Data_1
);

  wire and_1_out, demultiplexer_1_out1, demultiplexer_1_out2, demultiplexer_1_out3, demultiplexer_1_out4,
       demultiplexer_1_out6, demultiplexer_1_out7, not_1_out, not_2_out, not_3_out, not_4_out, not_5_out;

  Demultiplexer #(.select(3), .enable("false")) demultiplexer_1 (
    .out1(demultiplexer_1_out1), .out2(demultiplexer_1_out2), .out3(demultiplexer_1_out3),
    .out4(demultiplexer_1_out4), .out6(demultiplexer_1_out6), .out7(demultiplexer_1_out7), .in(and_1_out),
    .sel(Dst_Reg_1[2:0]));  // open: out0, out5
  and and_1 (and_1_out, RegWrite, CLK);
  not not_1 (not_1_out, demultiplexer_1_out1);
  not not_2 (not_2_out, demultiplexer_1_out2);
  not not_3 (not_3_out, demultiplexer_1_out3);
  not not_4 (not_4_out, demultiplexer_1_out4);
  Multiplexer #(.select(3), .width(4), .enable("false")) multiplexer_1 (
    .in0(4'b0000), .in1(t4__t3__t2__t1__t0__sp[7:4]), .in2(t4__t3__t2__t1__t0__sp[11:8]),
    .in3(t4__t3__t2__t1__t0__sp[15:12]), .in4(t4__t3__t2__t1__t0__sp[19:16]), .in5(4'b0000),
    .in6(t4__t3__t2__t1__t0__sp[23:20]), .in7(t4__t3__t2__t1__t0__sp[3:0]), .out(Read_Data_1),
    .sel(Src_Reg_1[2:0]));
  Register #(.width(4)) t1 (.D(Write_Data), .Q(t4__t3__t2__t1__t0__sp[7:4]), .clk(not_1_out), .clr(CLR));  // open: en
  Register #(.width(4)) t2 (.D(Write_Data), .Q(t4__t3__t2__t1__t0__sp[11:8]), .clk(not_2_out), .clr(CLR));  // open: en
  Register #(.width(4)) t3 (.D(Write_Data), .Q(t4__t3__t2__t1__t0__sp[15:12]), .clk(not_3_out), .clr(CLR));  // open: en
  Register #(.width(4)) t0 (
    .D(Write_Data), .Q(t4__t3__t2__t1__t0__sp[3:0]), .clk(demultiplexer_1_out7), .clr(CLR));  // open: en
  Multiplexer #(.select(3), .width(4), .enable("false")) multiplexer_2 (
    .in0(4'b0000), .in1(t4__t3__t2__t1__t0__sp[7:4]), .in2(t4__t3__t2__t1__t0__sp[11:8]),
    .in3(t4__t3__t2__t1__t0__sp[15:12]), .in4(t4__t3__t2__t1__t0__sp[19:16]), .in5(4'b0000),
    .in6(t4__t3__t2__t1__t0__sp[23:20]), .in7(t4__t3__t2__t1__t0__sp[3:0]), .out(Read_Data_2),
    .sel(SrcReg2[2:0]));
  Register #(.width(4)) t4 (.D(Write_Data), .Q(t4__t3__t2__t1__t0__sp[19:16]), .clk(not_4_out), .clr(CLR));  // open: en
  not not_5 (not_5_out, demultiplexer_1_out6);
  Register #(.width(4)) sp (.D(Write_Data), .Q(t4__t3__t2__t1__t0__sp[23:20]), .clk(not_5_out), .clr(CLR));  // open: en

  // Notes on the sheet:
  //   zero
endmodule

module Control_Unit (
  input  [3:0] OP_Code,
  output [2:0] ALUOp,
  output Jump,
  output bneq,
  output beq,
  output MemWrite,
  output MemRead,
  output RegWrite,
  output MemToReg,
  output ALUSrc,
  output RegDst
);

  ROM #(.addrWidth(4), .dataWidth(12)) rom_1 (
    .addr(OP_Code), .data({RegDst, ALUSrc, MemToReg, RegWrite, MemRead, MemWrite, beq, bneq, Jump, ALUOp}));  // open: sel

  // Notes on the sheet:
  //   contents of rom_1 (hex, n*v repeats v):
  //   901 11 903 500 505 904 900 503 8 640 506 902 501 780 502 21
endmodule

module Data_Memory (
  input  MemRead,
  input  MemWrite,
  input  [3:0] Address,
  input  [3:0] Write_Data,
  input  CLK,
  input  CLR,
  output [3:0] Data_Read
);

  wire not_1_out;

  not not_1 (not_1_out, CLK);
  RAM #(.addrWidth(4), .dataWidth(4), .bus("separate")) ram_1 (
    .addr(Address), .din(Write_Data), .data(Data_Read), .str(MemWrite), .clk(not_1_out), .ld(MemRead),
    .clr(CLR));  // open: sel
endmodule
