// Logisim project A2_Group5_IC_V2.circ as structural Verilog: 16 circuits, main circuit 12_bit_mux
module _12_bit_mux (
  input  [11:0] _12_bit_input_1,
  input  [11:0] _12_bit_input_2,
  input  Selection_bit,
  output [11:0] _12_bit_Mux_Output
);

  _74157 u_74157_1 (
    ._1__S(Selection_bit), ._2__A1(_12_bit_input_1[0]), ._3__B1(_12_bit_input_2[0]),
    ._4__Y1(_12_bit_Mux_Output[0]), ._5__A2(_12_bit_input_1[1]), ._6__B2(_12_bit_input_2[1]),
    ._7__Y2(_12_bit_Mux_Output[1]), ._8__GND(1'b0), ._16__Vcc(1'b1), ._15__G(1'b0),
    ._14__A4(_12_bit_input_1[2]), ._13__B4(_12_bit_input_2[2]), ._12__Y4(_12_bit_Mux_Output[2]),
    ._11__A3(_12_bit_input_1[3]), ._10__B3(_12_bit_input_2[3]), ._9__Y3(_12_bit_Mux_Output[3]));
  _74157 u_74157_2 (
    ._1__S(Selection_bit), ._2__A1(_12_bit_input_1[4]), ._3__B1(_12_bit_input_2[4]),
    ._4__Y1(_12_bit_Mux_Output[4]), ._5__A2(_12_bit_input_1[5]), ._6__B2(_12_bit_input_2[5]),
    ._7__Y2(_12_bit_Mux_Output[5]), ._8__GND(1'b0), ._16__Vcc(1'b1), ._15__G(1'b0),
    ._14__A4(_12_bit_input_1[6]), ._13__B4(_12_bit_input_2[6]), ._12__Y4(_12_bit_Mux_Output[6]),
    ._11__A3(_12_bit_input_1[7]), ._10__B3(_12_bit_input_2[7]), ._9__Y3(_12_bit_Mux_Output[7]));
  _74157 u_74157_3 (
    ._1__S(Selection_bit), ._2__A1(_12_bit_input_1[8]), ._3__B1(_12_bit_input_2[8]),
    ._4__Y1(_12_bit_Mux_Output[8]), ._5__A2(_12_bit_input_1[9]), ._6__B2(_12_bit_input_2[9]),
    ._7__Y2(_12_bit_Mux_Output[9]), ._8__GND(1'b0), ._16__Vcc(1'b1), ._15__G(1'b0),
    ._14__A4(_12_bit_input_1[10]), ._13__B4(_12_bit_input_2[10]), ._12__Y4(_12_bit_Mux_Output[10]),
    ._11__A3(_12_bit_input_1[11]), ._10__B3(_12_bit_input_2[11]), ._9__Y3(_12_bit_Mux_Output[11]));
endmodule

module _32_bit_Mux (
  input  [31:0] _32_bit_input_1,
  input  [31:0] _32_bit_input_2,
  input  Selection_bit,
  output [31:0] _32_bit_Mux_Output
);

  wire [11:8] n12_bit_mux_3__12_bit_mux_output;

  _12_bit_mux u_12_bit_mux_1 (
    ._12_bit_input_1(_32_bit_input_1[11:0]), ._12_bit_input_2(_32_bit_input_2[11:0]),
    .Selection_bit(Selection_bit), ._12_bit_Mux_Output(_32_bit_Mux_Output[11:0]));
  _12_bit_mux u_12_bit_mux_2 (
    ._12_bit_input_1(_32_bit_input_1[23:12]), ._12_bit_input_2(_32_bit_input_2[23:12]),
    .Selection_bit(Selection_bit), ._12_bit_Mux_Output(_32_bit_Mux_Output[23:12]));
  _12_bit_mux u_12_bit_mux_3 (
    ._12_bit_input_1({4'b0000, _32_bit_input_1[31:24]}), ._12_bit_input_2({4'b0000, _32_bit_input_2[31:24]}),
    .Selection_bit(Selection_bit),
    ._12_bit_Mux_Output({n12_bit_mux_3__12_bit_mux_output, _32_bit_Mux_Output[31:24]}));

  // Notes on the sheet:
  //   12 Bit MUX
  //   12 Bit MUX
  //   12 Bit MUX
endmodule

module rounding_mini (
  input  [31:0] _32_bit_Significand,
  output [31:0] _32_bit_Significand_Output
);

  wire n744075_1__6__2y, n744075_1__8__3y, n744075_1__12__1y, n744075_2__6__2y, n744075_2__8__3y;
  wire [11:11] n7408_1__11__4y;

  _744075 u_744075_1 (
    ._1__1A(_32_bit_Significand[0]), ._2__1B(_32_bit_Significand[1]), ._3__2A(_32_bit_Significand[3]),
    ._4__2B(_32_bit_Significand[4]), ._5__2C(_32_bit_Significand[5]), ._6__2Y(n744075_1__6__2y),
    ._7__GND(1'b0), ._14__Vcc(1'b1), ._13__1C(_32_bit_Significand[2]), ._12__1Y(n744075_1__12__1y),
    ._11__3C(_32_bit_Significand[6]), ._10__3B(_32_bit_Significand[7]), ._9__3A(_32_bit_Significand[8]),
    ._8__3Y(n744075_1__8__3y));
  _744075 u_744075_2 (
    ._3__2A(n744075_1__12__1y), ._4__2B(n744075_1__8__3y), ._5__2C(n744075_1__6__2y),
    ._6__2Y(n744075_2__6__2y), ._7__GND(1'b0), ._14__Vcc(1'b1), ._11__3C(_32_bit_Significand[11]),
    ._10__3B(_32_bit_Significand[9]), ._9__3A(n744075_2__6__2y), ._8__3Y(n744075_2__8__3y));  // open: _1__1A, _2__1B, _13__1C, _12__1Y
  _7408 u_7408_1 (
    ._7__GND(1'b0), ._14__Vcc(1'b1), ._13__4B(n744075_2__8__3y), ._12__4A(_32_bit_Significand[10]),
    ._11__4Y(n7408_1__11__4y[11]));  // open: _1__1A, _2__1B, _3__1Y, _4__2A, _5__2B, _6__2Y, _10__3B, _9__3A, _8__3Y
  Adder #(.width(32)) adder_1 (
    .a({{20{1'b0}}, n7408_1__11__4y[11], {11{1'b0}}}), .b(_32_bit_Significand),
    .out(_32_bit_Significand_Output), .cin(1'b0));  // open: cout

  // Notes on the sheet:
  //   S
  //   :
  //   L
  //   S
  //   R
  //   G
  //   R + L + S
  //   G (L+R+S)
  //   32 Bit Adder
endmodule

module rounding_circuit (
  input  [31:0] Significand,
  input  [11:0] Exponent,
  output [31:0] significand_2,
  output [11:0] Exponent_2,
  output Overflow
);

  wire [31:0] rounding_mini_1__32_bit_significand_output;

  rounding_mini rounding_mini_1 (
    ._32_bit_Significand(Significand), ._32_bit_Significand_Output(rounding_mini_1__32_bit_significand_output));
  Adder #(.width(12)) adder_1 (
    .a(Exponent), .b({12{1'b0}}), .out(Exponent_2), .cin(rounding_mini_1__32_bit_significand_output[31]));  // open: cout
  Shifter #(.width(32), .shift("lr")) shifter_1 (
    .in(rounding_mini_1__32_bit_significand_output),
    .\dist ({4'b0000, rounding_mini_1__32_bit_significand_output[31]}), .out(significand_2));
  _12_input_and u_12_input_and_1 (._12_bit_input(Exponent_2), .Output_1_bit(Overflow));

  // Notes on the sheet:
  //   Rounding mini circuit
  //   12 bit adder
  //   32 bit right shift
  //   12 Input AND Gate
endmodule

module _12_to_5_Bit_Shrinker (
  input  [11:0] _12_bit_input,
  output [4:0] _5_bit_lsb_output
);

  wire n744075_1__6__2y, n744075_1__8__3y, n744075_1__12__1y;

  _744075 u_744075_1 (
    ._1__1A(_12_bit_input[11]), ._2__1B(_12_bit_input[10]), ._3__2A(_12_bit_input[8]),
    ._4__2B(_12_bit_input[7]), ._5__2C(_12_bit_input[6]), ._6__2Y(n744075_1__6__2y), ._7__GND(1'b0),
    ._14__Vcc(1'b1), ._13__1C(_12_bit_input[9]), ._12__1Y(n744075_1__12__1y), ._11__3C(n744075_1__12__1y),
    ._10__3B(n744075_1__6__2y), ._9__3A(_12_bit_input[5]), ._8__3Y(n744075_1__8__3y));
  _74157 u_74157_1 (
    ._1__S(n744075_1__8__3y), ._2__A1(_12_bit_input[0]), ._3__B1(1'b1), ._4__Y1(_5_bit_lsb_output[0]),
    ._5__A2(_12_bit_input[1]), ._6__B2(1'b1), ._7__Y2(_5_bit_lsb_output[1]), ._8__GND(1'b0), ._16__Vcc(1'b1),
    ._15__G(1'b0), ._14__A4(_12_bit_input[2]), ._13__B4(1'b1), ._12__Y4(_5_bit_lsb_output[2]),
    ._11__A3(_12_bit_input[3]), ._10__B3(1'b1), ._9__Y3(_5_bit_lsb_output[3]));
  _74157 u_74157_2 (
    ._1__S(n744075_1__8__3y), ._2__A1(_12_bit_input[4]), ._3__B1(1'b1), ._4__Y1(_5_bit_lsb_output[4]),
    ._8__GND(1'b0), ._16__Vcc(1'b1), ._15__G(1'b0));  // open: _5__A2, _6__B2, _7__Y2, _14__A4, _13__B4, _12__Y4, _11__A3, _10__B3, _9__Y3
endmodule

module _5_to_12_Bit_padder (
  input  [4:0] _5_bit_input,
  output [11:0] _12_bit_output
);


  assign _12_bit_output = {{7{1'b0}}, _5_bit_input};
endmodule

module Set_bit_finder (
  input  [31:0] _32_bit_input,
  output [4:0] Shift_amount,
  output contains_one
);

  wire [4:0] bitfinder_1_index;

  BitFinder #(.width(32)) bitfinder_1 (
    .in({_32_bit_input[0], _32_bit_input[1], _32_bit_input[2], _32_bit_input[3], _32_bit_input[4], _32_bit_input[5], _32_bit_input[6], _32_bit_input[7], _32_bit_input[8], _32_bit_input[9], _32_bit_input[10], _32_bit_input[11], _32_bit_input[12], _32_bit_input[13], _32_bit_input[14], _32_bit_input[15], _32_bit_input[16], _32_bit_input[17], _32_bit_input[18], _32_bit_input[19], _32_bit_input[20], _32_bit_input[21], _32_bit_input[22], _32_bit_input[23], _32_bit_input[24], _32_bit_input[25], _32_bit_input[26], _32_bit_input[27], _32_bit_input[28], _32_bit_input[29], _32_bit_input[30], _32_bit_input[31]}),
    .index(bitfinder_1_index), .found(contains_one));
  Subtractor #(.width(5)) subtractor_1 (
    .a(bitfinder_1_index), .b({5{1'b0}}), .out(Shift_amount), .bin(1'b1));  // open: bout

  // Notes on the sheet:
  //   bit finder, finds indx of input's lowest order 1
  //   5 bit subtractor
endmodule

module _12_input_and (
  input  [11:0] _12_bit_input,
  output Output_1_bit
);

  wire n7421_1__6__1y, n7421_1__8__2y, n7421_2__6__1y;

  _7421 u_7421_1 (
    ._1__1A(_12_bit_input[0]), ._2__1B(_12_bit_input[1]), ._4__1C(_12_bit_input[2]),
    ._5__1D(_12_bit_input[3]), ._6__1Y(n7421_1__6__1y), ._7__GND(1'b0), ._14__Vcc(1'b1),
    ._13__2D(_12_bit_input[4]), ._12__2C(_12_bit_input[5]), ._10__2B(_12_bit_input[6]),
    ._9__2A(_12_bit_input[7]), ._8__2Y(n7421_1__8__2y));  // open: _3__NC, _11__NC
  _7421 u_7421_2 (
    ._1__1A(_12_bit_input[8]), ._2__1B(_12_bit_input[9]), ._4__1C(_12_bit_input[10]),
    ._5__1D(_12_bit_input[11]), ._6__1Y(n7421_2__6__1y), ._7__GND(1'b0), ._14__Vcc(1'b1),
    ._13__2D(n7421_2__6__1y), ._12__2C(n7421_1__8__2y), ._10__2B(n7421_1__6__1y), ._9__2A(1'b1),
    ._8__2Y(Output_1_bit));  // open: _3__NC, _11__NC
endmodule

module Normalizer (
  input  [11:0] Exponent,
  input  [31:0] Significand,
  output Significand_contains_one,
  output [31:0] Significand_output,
  output [11:0] Exponent_Output
);

  wire n12_bit_input_or_gate_1_output_1_bit, n12_input_and_1_output_1_bit, n12_input_and_2_output_1_bit,
       n7404_1__2__1y, n7408_1__3__1y, n7421_1__6__1y, n7421_1__8__2y, n7432_1__3__1y, n7486_1__3__1y,
       subtractor_1_bout;
  wire [4:0] n12_to_5_bit_shrinker_1__5_bit_lsb_output, set_bit_finder_1_shift_amount;
  wire [11:0] n5_to_12_bit_padder_1__12_bit_output, n12_bit_mux_1__12_bit_mux_output,
       n12_bit_mux_2__12_bit_mux_output, n12_bit_mux_4__12_bit_mux_output, subtractor_1_out, subtractor_2_out;
  wire [31:0] shifter_1_out;

  _12_input_and u_12_input_and_1 (._12_bit_input(Exponent), .Output_1_bit(n12_input_and_1_output_1_bit));
  Subtractor #(.width(12)) subtractor_1 (
    .a(Exponent), .b(n12_bit_mux_2__12_bit_mux_output), .out(subtractor_1_out), .bin(1'b0),
    .bout(subtractor_1_bout));
  _12_bit_input_or_gate u_12_bit_input_or_gate_1 (
    ._12_Bit_Input(subtractor_1_out), .Output_1_bit(n12_bit_input_or_gate_1_output_1_bit));
  _12_bit_mux u_12_bit_mux_1 (
    ._12_bit_input_1(subtractor_1_out), ._12_bit_input_2({12{1'b0}}), .Selection_bit(n7408_1__3__1y),
    ._12_bit_Mux_Output(n12_bit_mux_1__12_bit_mux_output));
  _12_bit_mux u_12_bit_mux_2 (
    ._12_bit_input_1(n5_to_12_bit_padder_1__12_bit_output), ._12_bit_input_2({12{1'b1}}),
    .Selection_bit(n7421_1__8__2y), ._12_bit_Mux_Output(n12_bit_mux_2__12_bit_mux_output));
  _7404 u_7404_1 (
    ._1__1A(n12_bit_input_or_gate_1_output_1_bit), ._2__1Y(n7404_1__2__1y), ._7__GND(1'b0), ._14__Vcc(1'b1));  // open: _3__2A, _4__2Y, _5__3A, _6__3Y, _13__6A, _12__6Y, _11__5A, _10__5Y, _9__4A, _8__4Y
  _12_bit_mux u_12_bit_mux_3 (
    ._12_bit_input_1(n12_bit_mux_1__12_bit_mux_output), ._12_bit_input_2({12{1'b1}}),
    .Selection_bit(n12_input_and_1_output_1_bit), ._12_bit_Mux_Output(Exponent_Output));
  _7432 u_7432_1 (
    ._1__1A(n7404_1__2__1y), ._2__1B(subtractor_1_bout), ._3__1Y(n7432_1__3__1y), ._7__GND(1'b0),
    ._14__Vcc(1'b1));  // open: _4__2A, _5__2B, _6__2Y, _13__4B, _12__4A, _11__4Y, _10__3B, _9__3A, _8__3Y
  Subtractor #(.width(12)) subtractor_2 (
    .a(Exponent), .b({12{1'b0}}), .out(subtractor_2_out), .bin(n7404_1__2__1y));  // open: bout
  _12_input_and u_12_input_and_2 (._12_bit_input(Exponent_Output), .Output_1_bit(n12_input_and_2_output_1_bit));
  _7408 u_7408_1 (
    ._1__1A(n7432_1__3__1y), ._2__1B(n7486_1__3__1y), ._3__1Y(n7408_1__3__1y), ._7__GND(1'b0), ._14__Vcc(1'b1));  // open: _4__2A, _5__2B, _6__2Y, _13__4B, _12__4A, _11__4Y, _10__3B, _9__3A, _8__3Y
  Set_bit_finder set_bit_finder_1 (
    ._32_bit_input(Significand), .Shift_amount(set_bit_finder_1_shift_amount),
    .contains_one(Significand_contains_one));
  _5_to_12_Bit_padder u_5_to_12_bit_padder_1 (
    ._5_bit_input(set_bit_finder_1_shift_amount), ._12_bit_output(n5_to_12_bit_padder_1__12_bit_output));
  _12_bit_mux u_12_bit_mux_4 (
    ._12_bit_input_1(n5_to_12_bit_padder_1__12_bit_output), ._12_bit_input_2(subtractor_2_out),
    .Selection_bit(n7408_1__3__1y), ._12_bit_Mux_Output(n12_bit_mux_4__12_bit_mux_output));
  _12_to_5_Bit_Shrinker u_12_to_5_bit_shrinker_1 (
    ._12_bit_input(n12_bit_mux_4__12_bit_mux_output),
    ._5_bit_lsb_output(n12_to_5_bit_shrinker_1__5_bit_lsb_output));
  _7486 u_7486_1 (
    ._1__1A(Significand[31]), ._2__1B(1'b1), ._3__1Y(n7486_1__3__1y), ._7__GND(1'b0), ._14__Vcc(1'b1));  // open: _4__2A, _5__2B, _6__2Y, _13__4B, _12__4A, _11__4Y, _10__3B, _9__3A, _8__3Y
  Shifter #(.width(32), .shift("rl")) shifter_1 (
    .in(Significand), .\dist (n12_to_5_bit_shrinker_1__5_bit_lsb_output), .out(shifter_1_out));
  _32_bit_Mux u_32_bit_mux_1 (
    ._32_bit_input_1({1'b0, shifter_1_out[30:0]}), ._32_bit_input_2(32'h40000000),
    .Selection_bit(n12_input_and_2_output_1_bit), ._32_bit_Mux_Output(Significand_output));
  _7421 u_7421_1 (
    ._1__1A(set_bit_finder_1_shift_amount[0]), ._2__1B(set_bit_finder_1_shift_amount[1]),
    ._4__1C(set_bit_finder_1_shift_amount[2]), ._5__1D(set_bit_finder_1_shift_amount[3]),
    ._6__1Y(n7421_1__6__1y), ._7__GND(1'b0), ._14__Vcc(1'b1), ._13__2D(1'b1), ._12__2C(1'b1),
    ._10__2B(n7421_1__6__1y), ._9__2A(set_bit_finder_1_shift_amount[4]), ._8__2Y(n7421_1__8__2y));  // open: _3__NC, _11__NC

  // Notes on the sheet:
  //   12 Input AND Gate
  //   12 bit subtractor
  //   12 Bit MUX
  //   12 Bit MUX
  //   12 Bit MUX
  //   12 Bit MUX
  //   12 Input AND Gate
  //   12 bit subtractor
  //   12 to 5 bit shrinker
  //   Set Bit Finder
  //   12 Bit Padder
  //   12 Bit MUX
  //   32 bit left rotator
  //   32 Bit MUX
endmodule

module _12_bit_input_or_gate (
  input  [11:0] _12_Bit_Input,
  output Output_1_bit
);

  wire n744075_1__6__2y, n744075_1__8__3y, n744075_1__12__1y, n744075_2__6__2y, n744075_2__8__3y;

  _744075 u_744075_1 (
    ._1__1A(_12_Bit_Input[7]), ._2__1B(_12_Bit_Input[8]), ._3__2A(_12_Bit_Input[9]),
    ._4__2B(_12_Bit_Input[10]), ._5__2C(_12_Bit_Input[11]), ._6__2Y(n744075_1__6__2y), ._7__GND(1'b0),
    ._14__Vcc(1'b1), ._13__1C(_12_Bit_Input[6]), ._12__1Y(n744075_1__12__1y), ._11__3C(_12_Bit_Input[5]),
    ._10__3B(_12_Bit_Input[4]), ._9__3A(_12_Bit_Input[3]), ._8__3Y(n744075_1__8__3y));
  _744075 u_744075_2 (
    ._1__1A(1'b0), ._2__1B(n744075_1__8__3y), ._3__2A(_12_Bit_Input[0]), ._4__2B(_12_Bit_Input[1]),
    ._5__2C(_12_Bit_Input[2]), ._6__2Y(n744075_2__6__2y), ._7__GND(1'b0), ._14__Vcc(1'b1),
    ._13__1C(n744075_2__8__3y), ._12__1Y(Output_1_bit), ._11__3C(n744075_1__12__1y),
    ._10__3B(n744075_1__6__2y), ._9__3A(n744075_2__6__2y), ._8__3Y(n744075_2__8__3y));
endmodule

module overflow_underflow_setter (
  input  [11:0] Exponent,
  input  All_bits_of_significant_are_not_zero,
  output Overflow,
  output Underflow
);

  wire _12_Input_OR_Gate_output_1_bit, n7404_1__2__1y;

  _12_input_and _12_Input_AND_Gate (._12_bit_input(Exponent), .Output_1_bit(Overflow));
  _12_bit_input_or_gate _12_Input_OR_Gate (._12_Bit_Input(Exponent), .Output_1_bit(_12_Input_OR_Gate_output_1_bit));
  _7404 u_7404_1 (
    ._1__1A(_12_Input_OR_Gate_output_1_bit), ._2__1Y(n7404_1__2__1y), ._7__GND(1'b0), ._14__Vcc(1'b1));  // open: _3__2A, _4__2Y, _5__3A, _6__3Y, _13__6A, _12__6Y, _11__5A, _10__5Y, _9__4A, _8__4Y
  _7408 u_7408_1 (
    ._1__1A(n7404_1__2__1y), ._2__1B(All_bits_of_significant_are_not_zero), ._3__1Y(Underflow),
    ._7__GND(1'b0), ._14__Vcc(1'b1));  // open: _4__2A, _5__2B, _6__2Y, _13__4B, _12__4A, _11__4Y, _10__3B, _9__3A, _8__3Y
endmodule

module _19_to_32_bit_padder (
  input  [30:0] in_1,
  output [31:0] out_2
);

  wire n744075_1__6__2y, n744075_1__8__3y, n744075_1__12__1y, n744075_2__6__2y, n744075_2__8__3y;

  _744075 u_744075_1 (
    ._1__1A(in_1[20]), ._2__1B(in_1[21]), ._3__2A(in_1[22]), ._4__2B(in_1[23]), ._5__2C(in_1[24]),
    ._6__2Y(n744075_1__6__2y), ._7__GND(1'b0), ._14__Vcc(1'b1), ._13__1C(in_1[19]),
    ._12__1Y(n744075_1__12__1y), ._11__3C(in_1[25]), ._10__3B(in_1[26]), ._9__3A(in_1[27]),
    ._8__3Y(n744075_1__8__3y));
  _744075 u_744075_2 (
    ._1__1A(1'b0), ._2__1B(n744075_2__6__2y), ._3__2A(in_1[28]), ._4__2B(in_1[29]), ._5__2C(in_1[30]),
    ._6__2Y(n744075_2__6__2y), ._7__GND(1'b0), ._14__Vcc(1'b1), ._13__1C(n744075_2__8__3y),
    ._12__1Y(out_2[30]), ._11__3C(n744075_1__12__1y), ._10__3B(n744075_1__6__2y), ._9__3A(n744075_1__8__3y),
    ._8__3Y(n744075_2__8__3y));

  assign {out_2[31], out_2[29:0]} = {1'b0, in_1[18:0], {11{1'b0}}};

  // Notes on the sheet:
  //   3 input or, checks if exp is non zero, sets second bit of result 
endmodule

module _12_Bit_comparator (
  input  [11:0] Exponent_B,
  input  [11:0] Exponent_A,
  output [11:0] Difference_of_Exp,
  output Exp_A___Exp_B
);

  wire [11:0] negator_1_out, subtractor_1_out;

  Subtractor #(.width(12)) subtractor_1 (
    .a(Exponent_B), .b(Exponent_A), .out(subtractor_1_out), .bin(1'b0), .bout(Exp_A___Exp_B));
  Negator #(.width(12)) negator_1 (.in(subtractor_1_out), .out(negator_1_out));
  _12_bit_mux _12_Bit_MUX (
    ._12_bit_input_1(subtractor_1_out), ._12_bit_input_2(negator_1_out), .Selection_bit(Exp_A___Exp_B),
    ._12_bit_Mux_Output(Difference_of_Exp));

  // Notes on the sheet:
  //   12 bit subtractor
  //   12 Bit Negator
endmodule

module _32_Bit_adder (
  input  [31:0] Significand_1,
  input  [31:0] Significand_2,
  input  Lower_num_sign,
  input  Higher_num_sign,
  output [31:0] _32_bit_significand,
  output sign_bit
);

  wire comparator_1_lt, n7486_1__6__2y;
  wire [31:0] n32_bit_mux_1__32_bit_mux_output, n32_bit_mux_2__32_bit_mux_output,
       n32_bit_mux_3__32_bit_mux_output, negator_1_out;

  Comparator #(.width(32)) comparator_1 (.a(Significand_1), .b(Significand_2), .lt(comparator_1_lt));  // open: gt, eq
  _7486 u_7486_1 (
    ._4__2A(Lower_num_sign), ._5__2B(Higher_num_sign), ._6__2Y(n7486_1__6__2y), ._7__GND(1'b0),
    ._14__Vcc(1'b1));  // open: _1__1A, _2__1B, _3__1Y, _13__4B, _12__4A, _11__4Y, _10__3B, _9__3A, _8__3Y
  _32_bit_Mux u_32_bit_mux_1 (
    ._32_bit_input_1(Significand_2), ._32_bit_input_2(Significand_1), .Selection_bit(comparator_1_lt),
    ._32_bit_Mux_Output(n32_bit_mux_1__32_bit_mux_output));
  _32_bit_Mux u_32_bit_mux_2 (
    ._32_bit_input_1(Significand_1), ._32_bit_input_2(Significand_2), .Selection_bit(comparator_1_lt),
    ._32_bit_Mux_Output(n32_bit_mux_2__32_bit_mux_output));
  Negator #(.width(32)) negator_1 (.in(n32_bit_mux_1__32_bit_mux_output), .out(negator_1_out));
  _74157 u_74157_1 (
    ._1__S(comparator_1_lt), ._2__A1(Lower_num_sign), ._3__B1(Higher_num_sign), ._4__Y1(sign_bit),
    ._8__GND(1'b0), ._16__Vcc(1'b1), ._15__G(1'b0));  // open: _5__A2, _6__B2, _7__Y2, _14__A4, _13__B4, _12__Y4, _11__A3, _10__B3, _9__Y3
  _32_bit_Mux u_32_bit_mux_3 (
    ._32_bit_input_1(n32_bit_mux_1__32_bit_mux_output), ._32_bit_input_2(negator_1_out),
    .Selection_bit(n7486_1__6__2y), ._32_bit_Mux_Output(n32_bit_mux_3__32_bit_mux_output));
  Adder #(.width(32)) adder_1 (
    .a(n32_bit_mux_3__32_bit_mux_output), .b(n32_bit_mux_2__32_bit_mux_output), .out(_32_bit_significand));  // open: cin, cout

  // Notes on the sheet:
  //   Compares if 1 < 2
  //   32 Bit Comparator
  //   32 Bit MUX
  //   32 Bit MUX
  //   32 bit negator
  //   32 Bit MUX
  //   32 Bit Adder
endmodule

module main (
  input  [31:0] Number_A,
  input  [31:0] Number_B,
  output [31:0] Output,
  output Overflow,
  output Underflow
);

  wire n12_bit_comparator_1_exp_a___exp_b, n74157_1__4__y1, n74157_1__12__y4,
       normalizer_1_significand_contains_one, overflow_underflow_setter_1_overflow,
       rounding_circuit_1_overflow;
  wire [4:0] n12_to_5_bit_shrinker_1__5_bit_lsb_output;
  wire [11:0] n12_bit_comparator_1_difference_of_exp, n12_bit_mux_1__12_bit_mux_output,
       normalizer_1_exponent_output;
  wire [31:0] n19_to_32_bit_padder_1_out_2, n19_to_32_bit_padder_2_out_2,
       n32_bit_adder_1__32_bit_significand, n32_bit_mux_1__32_bit_mux_output,
       n32_bit_mux_2__32_bit_mux_output, normalizer_1_significand_output, rounding_circuit_1_significand_2,
       shifter_1_out;

  _74157 u_74157_1 (
    ._1__S(n12_bit_comparator_1_exp_a___exp_b), ._2__A1(Number_B[31]), ._3__B1(Number_A[31]),
    ._4__Y1(n74157_1__4__y1), ._8__GND(1'b0), ._16__Vcc(1'b1), ._15__G(1'b0), ._14__A4(Number_A[31]),
    ._13__B4(Number_B[31]), ._12__Y4(n74157_1__12__y4));  // open: _5__A2, _6__B2, _7__Y2, _11__A3, _10__B3, _9__Y3
  _19_to_32_bit_padder u_19_to_32_bit_padder_1 (.in_1(Number_A[30:0]), .out_2(n19_to_32_bit_padder_1_out_2));
  _12_bit_mux u_12_bit_mux_1 (
    ._12_bit_input_1(Number_B[30:19]), ._12_bit_input_2(Number_A[30:19]),
    .Selection_bit(n12_bit_comparator_1_exp_a___exp_b), ._12_bit_Mux_Output(n12_bit_mux_1__12_bit_mux_output));
  rounding_circuit rounding_circuit_1 (
    .Significand(normalizer_1_significand_output), .Exponent(normalizer_1_exponent_output),
    .significand_2({rounding_circuit_1_significand_2[31:30], Output[18:0], rounding_circuit_1_significand_2[10:0]}),
    .Exponent_2(Output[30:19]), .Overflow(rounding_circuit_1_overflow));
  _32_Bit_adder u_32_bit_adder_1 (
    .Significand_1(shifter_1_out), .Significand_2(n32_bit_mux_1__32_bit_mux_output),
    .Lower_num_sign(n74157_1__12__y4), .Higher_num_sign(n74157_1__4__y1),
    ._32_bit_significand(n32_bit_adder_1__32_bit_significand), .sign_bit(Output[31]));
  Normalizer normalizer_1 (
    .Exponent(n12_bit_mux_1__12_bit_mux_output), .Significand(n32_bit_adder_1__32_bit_significand),
    .Exponent_Output(normalizer_1_exponent_output), .Significand_output(normalizer_1_significand_output),
    .Significand_contains_one(normalizer_1_significand_contains_one));
  _12_Bit_comparator u_12_bit_comparator_1 (
    .Exponent_B(Number_B[30:19]), .Exponent_A(Number_A[30:19]),
    .Difference_of_Exp(n12_bit_comparator_1_difference_of_exp),
    .Exp_A___Exp_B(n12_bit_comparator_1_exp_a___exp_b));
  overflow_underflow_setter overflow_underflow_setter_1 (
    .Exponent(normalizer_1_exponent_output),
    .All_bits_of_significant_are_not_zero(normalizer_1_significand_contains_one),
    .Overflow(overflow_underflow_setter_1_overflow), .Underflow(Underflow));
  _7432 u_7432_1 (
    ._1__1A(overflow_underflow_setter_1_overflow), ._2__1B(rounding_circuit_1_overflow), ._3__1Y(Overflow),
    ._7__GND(1'b0), ._14__Vcc(1'b1));  // open: _4__2A, _5__2B, _6__2Y, _13__4B, _12__4A, _11__4Y, _10__3B, _9__3A, _8__3Y
  _19_to_32_bit_padder u_19_to_32_bit_padder_2 (.in_1(Number_B[30:0]), .out_2(n19_to_32_bit_padder_2_out_2));
  _32_bit_Mux u_32_bit_mux_1 (
    ._32_bit_input_1(n19_to_32_bit_padder_2_out_2), ._32_bit_input_2(n19_to_32_bit_padder_1_out_2),
    .Selection_bit(n12_bit_comparator_1_exp_a___exp_b), ._32_bit_Mux_Output(n32_bit_mux_1__32_bit_mux_output));
  _12_to_5_Bit_Shrinker u_12_to_5_bit_shrinker_1 (
    ._12_bit_input(n12_bit_comparator_1_difference_of_exp),
    ._5_bit_lsb_output(n12_to_5_bit_shrinker_1__5_bit_lsb_output));
  _32_bit_Mux u_32_bit_mux_2 (
    ._32_bit_input_1(n19_to_32_bit_padder_1_out_2), ._32_bit_input_2(n19_to_32_bit_padder_2_out_2),
    .Selection_bit(n12_bit_comparator_1_exp_a___exp_b), ._32_bit_Mux_Output(n32_bit_mux_2__32_bit_mux_output));
  Shifter #(.width(32), .shift("lr")) shifter_1 (
    .in(n32_bit_mux_2__32_bit_mux_output), .\dist (n12_to_5_bit_shrinker_1__5_bit_lsb_output),
    .out(shifter_1_out));

  // Notes on the sheet:
  //   MUXs for signs
  //   32 bit padder
  //   12 Bit MUX
  //   1 bit sign, 12 bit exponent, 19 bit fraction
  //   32 bit adder
  //   Normalizer
  //   Rounder
  //   taking exact 19 bit
  //   12 Bit Comparator
  //   overflow underflow setter
  //   32 bit padder
  //   32 Bit MUX
  //   12 to 5 bit shrinker
  //   32 Bit MUX
  //   32 bit right shift
endmodule

module FPA (
  input  [31:0] Number_A,
  input  [31:0] Number_B,
  output Underflow,
  output Overflow,
  output [31:0] Output
);

  main main_1 (.Number_A(Number_A), .Number_B(Number_B), .Output(Output), .Overflow(Overflow), .Underflow(Underflow));

  // Notes on the sheet:
  //   FPA
endmodule
