// Logisim project asif_adder_32bit.circ as structural Verilog: 1 circuit, main circuit main
module main (
  input  [31:0] Significand_1,
  input  [31:0] Significand_2,
  input  in_3,
  input  in_4,
  output [31:0] out_5,
  output out_6
);

  wire comparator_1_lt, xor_1_out;
  wire [31:0] multiplexer_1_out, multiplexer_2_out, multiplexer_4_out, negator_1_out;

  Comparator #(.width(32)) comparator_1 (.a(Significand_1), .b(Significand_2), .lt(comparator_1_lt));  // open: gt, eq
  xor xor_1 (xor_1_out, in_3, in_4);
  Multiplexer #(.width(32), .enable("false")) multiplexer_1 (
    .in0(Significand_2), .in1(Significand_1), .out(multiplexer_1_out), .sel(comparator_1_lt));
  Multiplexer #(.width(32), .enable("false")) multiplexer_2 (
    .in0(Significand_1), .in1(Significand_2), .out(multiplexer_2_out), .sel(comparator_1_lt));
  Negator #(.width(32)) negator_1 (.in(multiplexer_1_out), .out(negator_1_out));
  Multiplexer #(.enable("false")) multiplexer_3 (.in0(in_3), .in1(in_4), .out(out_6), .sel(comparator_1_lt));
  Multiplexer #(.width(32), .enable("false")) multiplexer_4 (
    .in0(multiplexer_1_out), .in1(negator_1_out), .out(multiplexer_4_out), .sel(xor_1_out));
  Adder #(.width(32)) adder_1 (.a(multiplexer_4_out), .b(multiplexer_2_out), .out(out_5));  // open: cin, cout
endmodule
