// Logisim project asif_comparator_12bit.circ as structural Verilog: 1 circuit, main circuit main
module main (
  input  [11:0] B,
  input  [11:0] A,
  output [11:0] out_3,
  output out_4
);

  wire [11:0] negator_1_out, subtractor_1_out;

  Subtractor #(.width(12)) subtractor_1 (.a(B), .b(A), .out(subtractor_1_out), .bin(1'b0), .bout(out_4));
  Negator #(.width(12)) negator_1 (.in(subtractor_1_out), .out(negator_1_out));
  Multiplexer #(.width(12), .enable("false")) multiplexer_1 (
    .in0(subtractor_1_out), .in1(negator_1_out), .out(out_3), .sel(out_4));
endmodule
