// Logisim project alu2.1.circ as structural Verilog: 1 circuit, main circuit alu_ckt
module alu_ckt (
  input  A0,
  input  A1,
  input  A2,
  input  A3,
  input  B0,
  input  B1,
  input  B2,
  input  B3,
  input  S0,
  input  S1,
  input  S3
);

  wire n7400_1__3__1y, n7400_1__6__2y, n7400_1__8__3y, n7400_1__11__4y, n7404_1__2__1y, n7432_1__3__1y,
       n7432_2__3__1y, n7432_2__6__2y, n7432_2__8__3y, n7432_2__11__4y, n7483_1__2__s3, n7483_1__6__s2,
       n7483_1__9__s1, n7483_1__14__cout, n7483_1__15__s4, n7486_1__3__1y, n7486_1__6__2y, n7486_1__8__3y,
       n7486_1__11__4y, n7486_2__3__1y, n7486_2__6__2y, n7486_2__8__3y, n7486_2__11__4y, n74138_1__7__y7,
       n74138_1__9__y6, n74138_1__10__y5, n74138_1__11__y4, n74138_1__12__y3, n74138_1__13__y2,
       n74138_1__14__y1, n74138_1__15__y0, n74157_1__4__y1, n74157_1__7__y2, n74157_1__9__y3,
       n74157_1__12__y4, n74157_2__4__y1, n74157_2__7__y2, n74157_2__9__y3, n74157_2__12__y4;

  _74138 u_74138_1 (
    ._1__A(S3), ._2__B(S1), ._3__C(S0), ._4__G2A(1'b0), ._5__G2B(1'b0), ._6__G1(1'b1),
    ._7__Y7(n74138_1__7__y7), ._8__GND(1'b0), ._16__Vcc(1'b1), ._15__Y0(n74138_1__15__y0),
    ._14__Y1(n74138_1__14__y1), ._13__Y2(n74138_1__13__y2), ._12__Y3(n74138_1__12__y3),
    ._11__Y4(n74138_1__11__y4), ._10__Y5(n74138_1__10__y5), ._9__Y6(n74138_1__9__y6));
  _7400 u_7400_1 (
    ._1__1A(n74138_1__15__y0), ._2__1B(n74138_1__14__y1), ._3__1Y(n7400_1__3__1y), ._4__2A(n74138_1__13__y2),
    ._5__2B(n74138_1__12__y3), ._6__2Y(n7400_1__6__2y), ._7__GND(1'b0), ._14__Vcc(1'b1),
    ._13__4B(n74138_1__13__y2), ._12__4A(n74138_1__12__y3), ._11__4Y(n7400_1__11__4y),
    ._10__3B(n74138_1__9__y6), ._9__3A(n74138_1__7__y7), ._8__3Y(n7400_1__8__3y));
  _7432 u_7432_1 (
    ._1__1A(n7400_1__6__2y), ._2__1B(n7400_1__3__1y), ._3__1Y(n7432_1__3__1y), ._7__GND(1'b0), ._14__Vcc(1'b1));  // open: _4__2A, _5__2B, _6__2Y, _13__4B, _12__4A, _11__4Y, _10__3B, _9__3A, _8__3Y
  _7486 u_7486_1 (
    ._1__1A(B0), ._2__1B(n7400_1__8__3y), ._3__1Y(n7486_1__3__1y), ._4__2A(B1), ._5__2B(n7400_1__8__3y),
    ._6__2Y(n7486_1__6__2y), ._7__GND(1'b0), ._14__Vcc(1'b1), ._13__4B(B2), ._12__4A(n7400_1__8__3y),
    ._11__4Y(n7486_1__11__4y), ._10__3B(B3), ._9__3A(n7400_1__8__3y), ._8__3Y(n7486_1__8__3y));
  _7432 u_7432_2 (
    ._1__1A(A0), ._2__1B(B0), ._3__1Y(n7432_2__3__1y), ._4__2A(A1), ._5__2B(B1), ._6__2Y(n7432_2__6__2y),
    ._7__GND(1'b0), ._14__Vcc(1'b1), ._13__4B(A2), ._12__4A(B2), ._11__4Y(n7432_2__11__4y), ._10__3B(A3),
    ._9__3A(B3), ._8__3Y(n7432_2__8__3y));
  _7486 u_7486_2 (
    ._1__1A(A0), ._2__1B(n7400_1__11__4y), ._3__1Y(n7486_2__3__1y), ._4__2A(A1), ._5__2B(n7400_1__11__4y),
    ._6__2Y(n7486_2__6__2y), ._7__GND(1'b0), ._14__Vcc(1'b1), ._13__4B(A2), ._12__4A(n7400_1__11__4y),
    ._11__4Y(n7486_2__11__4y), ._10__3B(A3), ._9__3A(n7400_1__11__4y), ._8__3Y(n7486_2__8__3y));
  _74157 u_74157_1 (
    ._1__S(n7432_1__3__1y), ._2__A1(n7486_1__3__1y), ._3__B1(1'b0), ._4__Y1(n74157_1__4__y1),
    ._5__A2(n7486_1__6__2y), ._6__B2(1'b0), ._7__Y2(n74157_1__7__y2), ._8__GND(1'b0), ._16__Vcc(1'b1),
    ._15__G(1'b0), ._14__A4(n7486_1__8__3y), ._13__B4(1'b0), ._12__Y4(n74157_1__12__y4),
    ._11__A3(n7486_1__11__4y), ._10__B3(1'b0), ._9__Y3(n74157_1__9__y3));
  _74157 u_74157_2 (
    ._1__S(n74138_1__15__y0), ._2__A1(n7432_2__3__1y), ._3__B1(n7483_1__9__s1), ._4__Y1(n74157_2__4__y1),
    ._5__A2(n7432_2__6__2y), ._6__B2(n7483_1__6__s2), ._7__Y2(n74157_2__7__y2), ._8__GND(1'b0),
    ._16__Vcc(1'b1), ._15__G(1'b0), ._14__A4(n7432_2__8__3y), ._13__B4(n7483_1__15__s4),
    ._12__Y4(n74157_2__12__y4), ._11__A3(n7432_2__11__4y), ._10__B3(n7483_1__2__s3), ._9__Y3(n74157_2__9__y3));
  _7483 u_7483_1 (
    ._1__A4(n7486_2__8__3y), ._2__S3(n7483_1__2__s3), ._3__A3(n7486_2__11__4y), ._4__B3(n74157_1__9__y3),
    ._5__Vcc(1'b1), ._6__S2(n7483_1__6__s2), ._7__B2(n74157_1__7__y2), ._8__A2(n7486_2__6__2y),
    ._16__B4(n74157_1__12__y4), ._15__S4(n7483_1__15__s4), ._14__Cout(n7483_1__14__cout),
    ._13__Cin(n7404_1__2__1y), ._12__GND(1'b0), ._11__B1(n74157_1__4__y1), ._10__A1(n7486_2__3__1y),
    ._9__S1(n7483_1__9__s1));
  _7404 u_7404_1 (
    ._1__1A(n74138_1__10__y5), ._2__1Y(n7404_1__2__1y), ._7__GND(1'b0), ._14__Vcc(1'b1));  // open: _3__2A, _4__2Y, _5__3A, _6__3Y, _13__6A, _12__6Y, _11__5A, _10__5Y, _9__4A, _8__4Y

  // Notes on the sheet:
  //   condition 1
  //   select A
  //   select B
endmodule
