// Logisim project alu2_flags_IC.circ as structural Verilog: 1 circuit, main circuit alu_ckt
module alu_ckt (
  input  A0,
  input  A1,
  input  A2,
  input  A3,
  input  B0,
  input  B1,
  input  B2,
  input  B3,
  input  S0,
  input  S1,
  input  S2,
  output Flag_V,
  output Flag_C,
  output Flag_Z,
  output Flag_S,
  output F0,
  output F1,
  output F2,
  output F3,
  output C_out
);

  wire n7400_1__3__1y, n7400_1__6__2y, n7400_1__8__3y, n7400_1__11__4y, n7400_2__3__1y, n7400_2__6__2y,
       n7400_2__8__3y, n7400_2__11__4y, n7402_1__1__1y, n7402_1__10__3y, n7402_2__1__1y, n7402_2__4__2y,
       n7402_2__10__3y, n7408_1__6__2y, n7408_1__8__3y, n7408_1__11__4y, n7432_1__3__1y, n7432_1__6__2y,
       n7432_1__8__3y, n7432_1__11__4y, n7483_1__2__s3, n7483_1__6__s2, n7483_1__9__s1, n7483_1__15__s4,
       n7486_1__3__1y, n7486_1__6__2y, n7486_1__8__3y, n7486_1__11__4y, n7486_2__3__1y, n7486_2__6__2y,
       n7486_2__8__3y, n7486_2__11__4y, n74138_1__7__y7, n74138_1__9__y6, n74138_1__10__y5, n74138_1__11__y4,
       n74138_1__12__y3, n74138_1__13__y2, n74138_1__14__y1, n74138_1__15__y0, n74157_2__4__y1,
       n74157_2__7__y2, n74157_2__9__y3, n74157_2__12__y4;

  _74138 u_74138_1 (
    ._1__A(S0), ._2__B(S1), ._3__C(S2), ._4__G2A(1'b0), ._5__G2B(1'b0), ._6__G1(1'b1),
    ._7__Y7(n74138_1__7__y7), ._8__GND(1'b0), ._16__Vcc(1'b1), ._15__Y0(n74138_1__15__y0),
    ._14__Y1(n74138_1__14__y1), ._13__Y2(n74138_1__13__y2), ._12__Y3(n74138_1__12__y3),
    ._11__Y4(n74138_1__11__y4), ._10__Y5(n74138_1__10__y5), ._9__Y6(n74138_1__9__y6));
  _7432 u_7432_1 (
    ._1__1A(A0), ._2__1B(B0), ._3__1Y(n7432_1__3__1y), ._4__2A(A1), ._5__2B(B1), ._6__2Y(n7432_1__6__2y),
    ._7__GND(1'b0), ._14__Vcc(1'b1), ._13__4B(B3), ._12__4A(A3), ._11__4Y(n7432_1__11__4y), ._10__3B(B2),
    ._9__3A(A2), ._8__3Y(n7432_1__8__3y));
  _7400 u_7400_1 (
    ._1__1A(n74138_1__13__y2), ._2__1B(n74138_1__12__y3), ._3__1Y(n7400_1__3__1y), ._4__2A(n74138_1__9__y6),
    ._5__2B(n74138_1__7__y7), ._6__2Y(n7400_1__6__2y), ._7__GND(1'b0), ._14__Vcc(1'b1),
    ._13__4B(n74138_1__14__y1), ._12__4A(n74138_1__13__y2), ._11__4Y(n7400_1__11__4y),
    ._10__3B(n74138_1__12__y3), ._9__3A(n74138_1__10__y5), ._8__3Y(n7400_1__8__3y));
  _7400 u_7400_2 (
    ._1__1A(n7400_1__11__4y), ._2__1B(n7400_1__11__4y), ._3__1Y(n7400_2__3__1y), ._4__2A(n7400_1__8__3y),
    ._5__2B(n7400_1__8__3y), ._6__2Y(n7400_2__6__2y), ._14__Vcc(1'b1), ._13__4B(n7400_2__3__1y),
    ._12__4A(n7400_2__6__2y), ._11__4Y(n7400_2__11__4y), ._10__3B(n74138_1__10__y5),
    ._9__3A(n74138_1__10__y5), ._8__3Y(n7400_2__8__3y));  // open: _7__GND
  _7486 u_7486_1 (
    ._1__1A(A0), ._2__1B(n7400_1__3__1y), ._3__1Y(n7486_1__3__1y), ._4__2A(A1), ._5__2B(n7400_1__3__1y),
    ._6__2Y(n7486_1__6__2y), ._7__GND(1'b0), ._14__Vcc(1'b1), ._13__4B(A2), ._12__4A(n7400_1__3__1y),
    ._11__4Y(n7486_1__11__4y), ._10__3B(A3), ._9__3A(n7400_1__3__1y), ._8__3Y(n7486_1__8__3y));
  _74157 u_74157_1 (
    ._1__S(n74138_1__15__y0), ._2__A1(n7432_1__3__1y), ._3__B1(n7483_1__9__s1), ._4__Y1(F0),
    ._5__A2(n7432_1__6__2y), ._6__B2(n7483_1__6__s2), ._7__Y2(F1), ._8__GND(1'b0), ._16__Vcc(1'b1),
    ._15__G(1'b0), ._14__A4(n7432_1__11__4y), ._13__B4(n7483_1__15__s4), ._12__Y4(F3),
    ._11__A3(n7432_1__8__3y), ._10__B3(n7483_1__2__s3), ._9__Y3(F2));
  _7486 u_7486_2 (
    ._1__1A(B0), ._2__1B(n7400_1__6__2y), ._3__1Y(n7486_2__3__1y), ._4__2A(B1), ._5__2B(n7400_1__6__2y),
    ._6__2Y(n7486_2__6__2y), ._7__GND(1'b0), ._14__Vcc(1'b1), ._13__4B(B2), ._12__4A(n7400_1__6__2y),
    ._11__4Y(n7486_2__11__4y), ._10__3B(B3), ._9__3A(n7400_1__6__2y), ._8__3Y(n7486_2__8__3y));
  _74157 u_74157_2 (
    ._1__S(n7400_2__11__4y), ._2__A1(n7486_2__3__1y), ._3__B1(1'b0), ._4__Y1(n74157_2__4__y1),
    ._5__A2(n7486_2__6__2y), ._6__B2(1'b0), ._7__Y2(n74157_2__7__y2), ._8__GND(1'b0), ._16__Vcc(1'b1),
    ._15__G(1'b0), ._14__A4(n7486_2__8__3y), ._13__B4(1'b0), ._12__Y4(n74157_2__12__y4),
    ._11__A3(n7486_2__11__4y), ._10__B3(1'b0), ._9__Y3(n74157_2__9__y3));
  _7483 u_7483_1 (
    ._1__A4(n7486_1__8__3y), ._2__S3(n7483_1__2__s3), ._3__A3(n7486_1__11__4y), ._4__B3(n74157_2__9__y3),
    ._5__Vcc(1'b1), ._6__S2(n7483_1__6__s2), ._7__B2(n74157_2__7__y2), ._8__A2(n7486_1__6__2y),
    ._16__B4(n74157_2__12__y4), ._15__S4(n7483_1__15__s4), ._14__Cout(C_out), ._13__Cin(n7400_2__8__3y),
    ._12__GND(1'b0), ._11__B1(n74157_2__4__y1), ._10__A1(n7486_1__3__1y), ._9__S1(n7483_1__9__s1));
  _7402 u_7402_1 (
    ._1__1Y(n7402_1__1__1y), ._2__1A(F3), ._3__1B(F3), ._7__GND(1'b0), ._14__Vcc(1'b1), ._13__4Y(Flag_V),
    ._12__4B(n7402_1__10__3y), ._11__4A(n7402_1__10__3y), ._10__3Y(n7402_1__10__3y), ._9__3B(n7408_1__8__3y),
    ._8__3A(n7408_1__11__4y));  // open: _4__2Y, _5__2A, _6__2B
  _7408 u_7408_1 (
    ._1__1A(C_out), ._2__1B(n74138_1__15__y0), ._3__1Y(Flag_C), ._4__2A(A3), ._5__2B(B3),
    ._6__2Y(n7408_1__6__2y), ._7__GND(1'b0), ._14__Vcc(1'b1), ._13__4B(n7402_2__10__3y), ._12__4A(F3),
    ._11__4Y(n7408_1__11__4y), ._10__3B(n7408_1__6__2y), ._9__3A(n7402_1__1__1y), ._8__3Y(n7408_1__8__3y));
  _7402 u_7402_2 (
    ._1__1Y(n7402_2__1__1y), ._2__1A(F1), ._3__1B(n7402_2__4__2y), ._4__2Y(n7402_2__4__2y), ._5__2A(F2),
    ._6__2B(F3), ._7__GND(1'b0), ._14__Vcc(1'b1), ._13__4Y(Flag_Z), ._12__4B(n7402_2__1__1y), ._11__4A(F0),
    ._10__3Y(n7402_2__10__3y), ._9__3B(B3), ._8__3A(A3));

  assign Flag_S = F3;

  // Notes on the sheet:
  //   S2+S1+S0
  //   A0
  //   A1
  //   A2
  //   A3
  //   B0
  //   B1
  //   B2
  //   S0
  //   S1
  //   S2
  //   B3
endmodule
