// Logisim project alu3.3.circ as structural Verilog: 2 circuits, main circuit alu_ckt
module alu_ckt (
  input  CS2,
  input  CS1,
  input  CS0,
  input  A3,
  input  A2,
  input  A1,
  input  A0,
  input  B3,
  input  B2,
  input  B1,
  input  B0,
  output F3,
  output F2,
  output F1,
  output F0,
  output V,
  output Z,
  output C,
  output S
);

  wire n7408_1__3__1y, n7408_1__6__2y, n7408_1__8__3y, n7408_1__11__4y, n7408_2__3__1y, n7408_2__6__2y,
       n7408_2__8__3y, n7408_2__11__4y, n7432_1__3__1y, n7432_1__6__2y, n7432_1__11__4y, n7432_2__8__3y,
       n7432_3__3__1y, n7432_3__6__2y, n7432_3__8__3y, n7432_3__11__4y, n7483_1__2__s3, n7483_1__6__s2,
       n7483_1__9__s1, n7483_1__15__s4, n7486_1__3__1y, n7486_1__6__2y, n7486_1__8__3y, n7486_1__11__4y,
       n7486_2__3__1y, n7486_2__6__2y, n7486_3__3__1y, n7486_3__6__2y, n7486_3__8__3y, n7486_3__11__4y,
       n74238_1__7__y7, n74238_1__9__y6, n74238_1__10__y5, n74238_1__11__y4, n74238_1__12__y3,
       n74238_1__13__y2, n74238_1__15__y0;

  _74238 u_74238_1 (
    ._1__A0(CS0), ._2__A1(CS1), ._3__A2(CS2), ._4__E1_prime(1'b0), ._5__E2_prime(1'b0), ._6__E3(1'b1),
    ._7__Y7(n74238_1__7__y7), ._8__GND(1'b0), ._16__Vcc(1'b1), ._15__Y0(n74238_1__15__y0),
    ._13__Y2(n74238_1__13__y2), ._12__Y3(n74238_1__12__y3), ._11__Y4(n74238_1__11__y4),
    ._10__Y5(n74238_1__10__y5), ._9__Y6(n74238_1__9__y6));  // open: _14__Y1
  _7408 u_7408_1 (
    ._1__1A(B3), ._2__1B(n74238_1__15__y0), ._3__1Y(n7408_1__3__1y), ._4__2A(B2), ._5__2B(n74238_1__15__y0),
    ._6__2Y(n7408_1__6__2y), ._7__GND(1'b0), ._14__Vcc(1'b1), ._13__4B(B1), ._12__4A(n74238_1__15__y0),
    ._11__4Y(n7408_1__11__4y), ._10__3B(B0), ._9__3A(n74238_1__15__y0), ._8__3Y(n7408_1__8__3y));
  _7432 u_7432_1 (
    ._1__1A(n74238_1__9__y6), ._2__1B(n74238_1__7__y7), ._3__1Y(n7432_1__3__1y), ._4__2A(n7432_1__3__1y),
    ._5__2B(n74238_1__11__y4), ._6__2Y(n7432_1__6__2y), ._7__GND(1'b0), ._14__Vcc(1'b1),
    ._13__4B(n74238_1__12__y3), ._12__4A(n74238_1__13__y2), ._11__4Y(n7432_1__11__4y),
    ._10__3B(n7483_1__6__s2), ._9__3A(n7408_1__11__4y), ._8__3Y(F1));
  _7432 u_7432_2 (
    ._1__1A(n7483_1__15__s4), ._2__1B(n7408_1__3__1y), ._3__1Y(F3), ._4__2A(n7483_1__2__s3),
    ._5__2B(n7408_1__6__2y), ._6__2Y(F2), ._7__GND(1'b0), ._14__Vcc(1'b1), ._13__4B(n7483_1__9__s1),
    ._12__4A(n7408_1__8__3y), ._11__4Y(F0), ._10__3B(F3), ._9__3A(F2), ._8__3Y(n7432_2__8__3y));
  _7486 u_7486_1 (
    ._1__1A(A3), ._2__1B(n7432_1__11__4y), ._3__1Y(n7486_1__3__1y), ._4__2A(A2), ._5__2B(n7432_1__11__4y),
    ._6__2Y(n7486_1__6__2y), ._7__GND(1'b0), ._14__Vcc(1'b1), ._13__4B(A1), ._12__4A(n7432_1__11__4y),
    ._11__4Y(n7486_1__11__4y), ._10__3B(A0), ._9__3A(n7432_1__11__4y), ._8__3Y(n7486_1__8__3y));
  _7432 u_7432_3 (
    ._1__1A(n7408_1__3__1y), ._2__1B(n7408_2__3__1y), ._3__1Y(n7432_3__3__1y), ._4__2A(C), ._5__2B(F3),
    ._6__2Y(n7432_3__6__2y), ._7__GND(1'b0), ._14__Vcc(1'b1), ._13__4B(n7432_2__8__3y),
    ._12__4A(n7432_3__8__3y), ._11__4Y(n7432_3__11__4y), ._10__3B(F1), ._9__3A(F0), ._8__3Y(n7432_3__8__3y));
  _7486 u_7486_2 (
    ._1__1A(n7486_1__3__1y), ._2__1B(n7432_3__3__1y), ._3__1Y(n7486_2__3__1y), ._4__2A(F3),
    ._5__2B(n7432_3__6__2y), ._6__2Y(n7486_2__6__2y), ._7__GND(1'b0), ._14__Vcc(1'b1),
    ._13__4B(n7432_3__11__4y), ._12__4A(1'b1), ._11__4Y(Z), ._10__3B(n7486_2__6__2y),
    ._9__3A(n7486_2__3__1y), ._8__3Y(V));
  _7486 u_7486_3 (
    ._1__1A(B3), ._2__1B(n7432_1__3__1y), ._3__1Y(n7486_3__3__1y), ._4__2A(B2), ._5__2B(n7432_1__3__1y),
    ._6__2Y(n7486_3__6__2y), ._7__GND(1'b0), ._14__Vcc(1'b1), ._13__4B(B1), ._12__4A(n7432_1__3__1y),
    ._11__4Y(n7486_3__11__4y), ._10__3B(B0), ._9__3A(n7432_1__3__1y), ._8__3Y(n7486_3__8__3y));
  _7408 u_7408_2 (
    ._1__1A(n7486_3__3__1y), ._2__1B(n7432_1__6__2y), ._3__1Y(n7408_2__3__1y), ._4__2A(n7486_3__6__2y),
    ._5__2B(n7432_1__6__2y), ._6__2Y(n7408_2__6__2y), ._7__GND(1'b0), ._14__Vcc(1'b1),
    ._13__4B(n7486_3__11__4y), ._12__4A(n7432_1__6__2y), ._11__4Y(n7408_2__11__4y), ._10__3B(n7486_3__8__3y),
    ._9__3A(n7432_1__6__2y), ._8__3Y(n7408_2__8__3y));
  _7483 u_7483_1 (
    ._1__A4(n7486_1__3__1y), ._2__S3(n7483_1__2__s3), ._3__A3(n7486_1__6__2y), ._4__B3(n7408_2__6__2y),
    ._5__Vcc(1'b1), ._6__S2(n7483_1__6__s2), ._7__B2(n7408_2__11__4y), ._8__A2(n7486_1__11__4y),
    ._16__B4(n7408_2__3__1y), ._15__S4(n7483_1__15__s4), ._14__Cout(C), ._13__Cin(n74238_1__10__y5),
    ._12__GND(1'b0), ._11__B1(n7408_2__8__3y), ._10__A1(n7486_1__8__3y), ._9__S1(n7483_1__9__s1));

  assign S = F3;

  // Notes on the sheet:
  //   S3
  //   S1
  //   S0
endmodule

module alu_block (
  input  S2,
  input  S1,
  input  S0,
  input  A3,
  input  A2,
  input  A1,
  input  A0,
  input  B3,
  input  B2,
  input  B1,
  input  B0,
  output F3,
  output F3_2,
  output F3_3,
  output F3_4,
  output Flag_V,
  output Flag_Z,
  output Flag_C,
  output Flag_S
);

  alu_ckt alu_ckt_1 (
    .A3(A3), .A2(A2), .A1(A1), .A0(A0), .B3(B3), .B2(B2), .B1(B1), .B0(B0), .CS2(S2), .CS1(S1), .CS0(S0),
    .V(Flag_V), .Z(Flag_Z), .C(Flag_C), .S(Flag_S), .F3(F3), .F2(F3_2), .F1(F3_3), .F0(F3_4));
endmodule
