// Logisim project padder.circ as structural Verilog
module _32_Bit_Padder (
  input  [30:0] in_1,
  output [31:0] out_2
);

  or Or___11 (out_2[30], in_1[19], in_1[20], in_1[21], in_1[22], in_1[23], in_1[24], in_1[25], in_1[26], in_1[27], in_1[28], in_1[29], in_1[30]);

  assign {out_2[31], out_2[29:0]} = {1'b0, in_1[18:0], {11{1'b0}}};

  // Notes on the sheet:
  //   this or checks if exp non zero
endmodule

module _32_bit_padder_ic (
  input  [30:0] in_1,
  output [31:0] out_2
);

  wire n744075_1__6__2y, n744075_1__8__3y, n744075_1__12__1y, n744075_2__6__2y, n744075_2__8__3y;

  _744075 u_744075_1 (
    ._1__1A(in_1[20]), ._2__1B(in_1[21]), ._3__2A(in_1[22]), ._4__2B(in_1[23]), ._5__2C(in_1[24]),
    ._6__2Y(n744075_1__6__2y), ._7__GND(1'b0), ._14__Vcc(1'b1), ._13__1C(in_1[19]),
    ._12__1Y(n744075_1__12__1y), ._11__3C(in_1[25]), ._10__3B(in_1[26]), ._9__3A(in_1[27]),
    ._8__3Y(n744075_1__8__3y));
  _744075 u_744075_2 (
    ._1__1A(1'b0), ._2__1B(n744075_2__6__2y), ._3__2A(in_1[28]), ._4__2B(in_1[29]), ._5__2C(in_1[30]),
    ._6__2Y(n744075_2__6__2y), ._7__GND(1'b0), ._14__Vcc(1'b1), ._13__1C(n744075_2__8__3y),
    ._12__1Y(out_2[30]), ._11__3C(n744075_1__12__1y), ._10__3B(n744075_1__6__2y), ._9__3A(n744075_1__8__3y),
    ._8__3Y(n744075_2__8__3y));

  assign {out_2[31], out_2[29:0]} = {1'b0, in_1[18:0], {11{1'b0}}};

  // Notes on the sheet:
  //   3 input or, checks if exp is non zero, sets second bit of result 
endmodule
